// Logisim project basicgates.circ as structural Verilog: 26 circuits, main circuit main
module main (
);

  wire adder128bit_1_overflow, subtractor128bit_1_borrow;
  wire [63:0] adder128bit_1_output1a, adder128bit_1_output1b, negate128bit_1_output1a,
       negate128bit_1_output1b, subtractor128bit_1_output1a, subtractor128bit_1_output1b;

  // Probe on adder128bit_1_overflow
  adder128bit adder128bit_1 (
    .inflow(1'b1), .input1a({64{1'b1}}), .input1b({64{1'b0}}), .input2a({64{1'b1}}), .input2b({64{1'b0}}),
    .overflow(adder128bit_1_overflow), .output1a(adder128bit_1_output1a), .output1b(adder128bit_1_output1b));
  // Probe on adder128bit_1_output1a
  // Probe on adder128bit_1_output1b
  // Probe on negate128bit_1_output1a
  negate128bit negate128bit_1 (
    .input1a({64{1'b1}}), .input1b({64{1'b0}}), .output1a(negate128bit_1_output1a),
    .output1b(negate128bit_1_output1b));
  // Probe on negate128bit_1_output1b
  // Probe on subtractor128bit_1_borrow
  subtractor128bit subtractor128bit_1 (
    .inborrow(1'b1), .input1a({64{1'b1}}), .input1b({64{1'b0}}), .input2a({64{1'b1}}), .input2b({64{1'b0}}),
    .borrow(subtractor128bit_1_borrow), .output1a(subtractor128bit_1_output1a),
    .output1b(subtractor128bit_1_output1b));
  // Probe on subtractor128bit_1_output1a
  // Probe on subtractor128bit_1_output1b
endmodule

module adder1bit (
  input  inflow,
  input  input1,
  input  input2,
  output overflow,
  output output1
);

  wire and_1_out, and_2_out, xor_1_out;

  and and_1 (and_1_out, input1, input2);
  xor xor_1 (xor_1_out, input1, input2);
  and and_2 (and_2_out, inflow, xor_1_out);
  xor xor_2 (output1, inflow, xor_1_out);
  or or_1 (overflow, and_1_out, and_2_out);
endmodule

module adder2bit (
  input  inflow,
  input  [1:0] input1,
  input  [1:0] input2,
  output overflow,
  output [1:0] output1
);

  wire adder1bit_1_overflow;

  adder1bit adder1bit_1 (
    .inflow(inflow), .input1(input1[0]), .input2(input2[0]), .overflow(adder1bit_1_overflow),
    .output1(output1[0]));
  adder1bit adder1bit_2 (
    .inflow(adder1bit_1_overflow), .input1(input1[1]), .input2(input2[1]), .overflow(overflow),
    .output1(output1[1]));
endmodule

module adder4bit (
  input  inflow,
  input  [3:0] input1,
  input  [3:0] input2,
  output overflow,
  output [3:0] output1
);

  wire adder2bit_1_overflow;

  adder2bit adder2bit_1 (
    .inflow(inflow), .input1(input1[1:0]), .input2(input2[1:0]), .overflow(adder2bit_1_overflow),
    .output1(output1[1:0]));
  adder2bit adder2bit_2 (
    .inflow(adder2bit_1_overflow), .input1(input1[3:2]), .input2(input2[3:2]), .overflow(overflow),
    .output1(output1[3:2]));
endmodule

module adder8bit (
  input  inflow,
  input  [7:0] input1,
  input  [7:0] input2,
  output overflow,
  output [7:0] output1
);

  wire adder4bit_1_overflow;

  adder4bit adder4bit_1 (
    .inflow(inflow), .input1(input1[3:0]), .input2(input2[3:0]), .overflow(adder4bit_1_overflow),
    .output1(output1[3:0]));
  adder4bit adder4bit_2 (
    .inflow(adder4bit_1_overflow), .input1(input1[7:4]), .input2(input2[7:4]), .overflow(overflow),
    .output1(output1[7:4]));
endmodule

module adder16bit (
  input  inflow,
  input  [15:0] input1,
  input  [15:0] input2,
  output overflow,
  output [15:0] output1
);

  wire adder8bit_1_overflow;

  adder8bit adder8bit_1 (
    .inflow(inflow), .input1(input1[7:0]), .input2(input2[7:0]), .overflow(adder8bit_1_overflow),
    .output1(output1[7:0]));
  adder8bit adder8bit_2 (
    .inflow(adder8bit_1_overflow), .input1(input1[15:8]), .input2(input2[15:8]), .overflow(overflow),
    .output1(output1[15:8]));
endmodule

module adder32bit (
  input  inflow,
  input  [31:0] input1,
  input  [31:0] input2,
  output overflow,
  output [31:0] output1
);

  wire adder16bit_1_overflow;

  adder16bit adder16bit_1 (
    .inflow(inflow), .input1(input1[15:0]), .input2(input2[15:0]), .overflow(adder16bit_1_overflow),
    .output1(output1[15:0]));
  adder16bit adder16bit_2 (
    .inflow(adder16bit_1_overflow), .input1(input1[31:16]), .input2(input2[31:16]), .overflow(overflow),
    .output1(output1[31:16]));
endmodule

module adder64bit (
  input  inflow,
  input  [63:0] input1,
  input  [63:0] input2,
  output overflow,
  output [63:0] output1
);

  wire adder32bit_1_overflow;

  adder32bit adder32bit_1 (
    .inflow(inflow), .input1(input1[31:0]), .input2(input2[31:0]), .overflow(adder32bit_1_overflow),
    .output1(output1[31:0]));
  adder32bit adder32bit_2 (
    .inflow(adder32bit_1_overflow), .input1(input1[63:32]), .input2(input2[63:32]), .overflow(overflow),
    .output1(output1[63:32]));
endmodule

module negate1bit (
  input  input1,
  output output1
);


  assign output1 = input1;
endmodule

module negate2bit (
  input  [1:0] input1,
  output [1:0] output1
);

  wire [1:0] not_1_out;

  assign not_1_out = ~input1;  // NOT_Gate not_1, 2 bits wide
  adder2bit adder2bit_1 (.input1(2'b01), .input2(not_1_out), .output1(output1));  // open: inflow, overflow
endmodule

module negate4bit (
  input  [3:0] input1,
  output [3:0] output1
);

  wire [3:0] not_1_out;

  assign not_1_out = ~input1;  // NOT_Gate not_1, 4 bits wide
  adder4bit adder4bit_1 (.input1(4'b0001), .input2(not_1_out), .output1(output1));  // open: inflow, overflow
endmodule

module negate8bit (
  input  [7:0] input1,
  output [7:0] output1
);

  wire [7:0] not_1_out;

  assign not_1_out = ~input1;  // NOT_Gate not_1, 8 bits wide
  adder8bit adder8bit_1 (.input1(8'h1), .input2(not_1_out), .output1(output1));  // open: inflow, overflow
endmodule

module negate16bit (
  input  [15:0] input1,
  output [15:0] output1
);

  wire [15:0] not_1_out;

  assign not_1_out = ~input1;  // NOT_Gate not_1, 16 bits wide
  adder16bit adder16bit_1 (.input1(16'h1), .input2(not_1_out), .output1(output1));  // open: inflow, overflow
endmodule

module negate32bit (
  input  [31:0] input1,
  output [31:0] output1
);

  wire [31:0] not_1_out;

  assign not_1_out = ~input1;  // NOT_Gate not_1, 32 bits wide
  adder32bit adder32bit_1 (.input1(32'h1), .input2(not_1_out), .output1(output1));  // open: inflow, overflow
endmodule

module negate64bit (
  input  [63:0] input1,
  output [63:0] output1
);

  wire [63:0] not_1_out;

  assign not_1_out = ~input1;  // NOT_Gate not_1, 64 bits wide
  adder64bit adder64bit_1 (.input1(64'h1), .input2(not_1_out), .output1(output1));  // open: inflow, overflow
endmodule

module subtractor1bit (
  input  inborrow,
  input  input1,
  input  input2,
  output borrow,
  output output1
);

  wire and_1_out, and_2_out, not_1_out, not_2_out, xor_1_out;

  not not_1 (not_1_out, input1);
  xor xor_1 (xor_1_out, input1, input2);
  and and_1 (and_1_out, not_1_out, input2);
  and and_2 (and_2_out, inborrow, not_2_out);
  not not_2 (not_2_out, xor_1_out);
  xor xor_2 (output1, inborrow, xor_1_out);
  or or_1 (borrow, and_1_out, and_2_out);
endmodule

module subtractor2bit (
  input  inborrow,
  input  [1:0] input1,
  input  [1:0] input2,
  output borrow,
  output [1:0] output1
);

  wire subtractor1bit_1_borrow;

  subtractor1bit subtractor1bit_1 (
    .inborrow(inborrow), .input1(input1[0]), .input2(input2[0]), .borrow(subtractor1bit_1_borrow),
    .output1(output1[0]));
  subtractor1bit subtractor1bit_2 (
    .inborrow(subtractor1bit_1_borrow), .input1(input1[1]), .input2(input2[1]), .borrow(borrow),
    .output1(output1[1]));
endmodule

module subtractor4bit (
  input  inborrow,
  input  [3:0] input1,
  input  [3:0] input2,
  output borrow,
  output [3:0] output1
);

  wire subtractor2bit_1_borrow;

  subtractor2bit subtractor2bit_1 (
    .inborrow(inborrow), .input1(input1[1:0]), .input2(input2[1:0]), .borrow(subtractor2bit_1_borrow),
    .output1(output1[1:0]));
  subtractor2bit subtractor2bit_2 (
    .inborrow(subtractor2bit_1_borrow), .input1(input1[3:2]), .input2(input2[3:2]), .borrow(borrow),
    .output1(output1[3:2]));
endmodule

module subtractor8bit (
  input  inborrow,
  input  [7:0] input1,
  input  [7:0] input2,
  output borrow,
  output [7:0] output1
);

  wire subtractor4bit_1_borrow;

  subtractor4bit subtractor4bit_1 (
    .inborrow(inborrow), .input1(input1[3:0]), .input2(input2[3:0]), .borrow(subtractor4bit_1_borrow),
    .output1(output1[3:0]));
  subtractor4bit subtractor4bit_2 (
    .inborrow(subtractor4bit_1_borrow), .input1(input1[7:4]), .input2(input2[7:4]), .borrow(borrow),
    .output1(output1[7:4]));
endmodule

module subtractor16bit (
  input  inborrow,
  input  [15:0] input1,
  input  [15:0] input2,
  output borrow,
  output [15:0] output1
);

  wire subtractor8bit_1_borrow;

  subtractor8bit subtractor8bit_1 (
    .inborrow(inborrow), .input1(input1[7:0]), .input2(input2[7:0]), .borrow(subtractor8bit_1_borrow),
    .output1(output1[7:0]));
  subtractor8bit subtractor8bit_2 (
    .inborrow(subtractor8bit_1_borrow), .input1(input1[15:8]), .input2(input2[15:8]), .borrow(borrow),
    .output1(output1[15:8]));
endmodule

module subtractor32bit (
  input  inborrow,
  input  [31:0] input1,
  input  [31:0] input2,
  output borrow,
  output [31:0] output1
);

  wire subtractor16bit_1_borrow;

  subtractor16bit subtractor16bit_1 (
    .inborrow(inborrow), .input1(input1[15:0]), .input2(input2[15:0]), .borrow(subtractor16bit_1_borrow),
    .output1(output1[15:0]));
  subtractor16bit subtractor16bit_2 (
    .inborrow(subtractor16bit_1_borrow), .input1(input1[31:16]), .input2(input2[31:16]), .borrow(borrow),
    .output1(output1[31:16]));
endmodule

module subtractor64bit (
  input  inborrow,
  input  [63:0] input1,
  input  [63:0] input2,
  output borrow,
  output [63:0] output1
);

  wire subtractor32bit_1_borrow;

  subtractor32bit subtractor32bit_1 (
    .inborrow(inborrow), .input1(input1[31:0]), .input2(input2[31:0]), .borrow(subtractor32bit_1_borrow),
    .output1(output1[31:0]));
  subtractor32bit subtractor32bit_2 (
    .inborrow(subtractor32bit_1_borrow), .input1(input1[63:32]), .input2(input2[63:32]), .borrow(borrow),
    .output1(output1[63:32]));
endmodule

module multiplier64bit (
  input  [63:0] input1,
  input  [63:0] input2,
  output [63:0] output1
);

  wire [63:0] adder64bit_1_output1, adder64bit_2_output1, adder64bit_3_output1, adder64bit_4_output1,
       adder64bit_5_output1, adder64bit_6_output1, adder64bit_7_output1, adder64bit_8_output1,
       adder64bit_9_output1, adder64bit_10_output1, adder64bit_11_output1, adder64bit_12_output1,
       adder64bit_13_output1, adder64bit_14_output1, adder64bit_15_output1, adder64bit_16_output1,
       adder64bit_17_output1, adder64bit_18_output1, adder64bit_19_output1, adder64bit_20_output1,
       adder64bit_21_output1, adder64bit_22_output1, adder64bit_23_output1, adder64bit_24_output1,
       adder64bit_25_output1, adder64bit_26_output1, adder64bit_28_output1, adder64bit_29_output1,
       adder64bit_30_output1, adder64bit_31_output1, adder64bit_32_output1, adder64bit_33_output1,
       adder64bit_34_output1, adder64bit_35_output1, adder64bit_36_output1, adder64bit_37_output1,
       adder64bit_38_output1, adder64bit_39_output1, adder64bit_40_output1, adder64bit_41_output1,
       adder64bit_42_output1, adder64bit_43_output1, adder64bit_44_output1, adder64bit_45_output1,
       adder64bit_46_output1, adder64bit_47_output1, adder64bit_48_output1, adder64bit_49_output1,
       adder64bit_50_output1, adder64bit_51_output1, adder64bit_52_output1, adder64bit_53_output1,
       adder64bit_54_output1, adder64bit_55_output1, adder64bit_56_output1, adder64bit_57_output1,
       adder64bit_58_output1, adder64bit_59_output1, adder64bit_60_output1, adder64bit_61_output1,
       adder64bit_62_output1, adder64bit_63_output1, pull_resistor_1_node, pull_resistor_2_node,
       pull_resistor_3_node, pull_resistor_4_node, pull_resistor_5_node, pull_resistor_6_node,
       pull_resistor_7_node, pull_resistor_8_node, pull_resistor_9_node, pull_resistor_10_node,
       pull_resistor_11_node, pull_resistor_12_node, pull_resistor_13_node, pull_resistor_14_node,
       pull_resistor_15_node, pull_resistor_16_node, pull_resistor_17_node, pull_resistor_18_node,
       pull_resistor_19_node, pull_resistor_20_node, pull_resistor_21_node, pull_resistor_22_node,
       pull_resistor_23_node, pull_resistor_24_node, pull_resistor_25_node, pull_resistor_26_node,
       pull_resistor_27_node, pull_resistor_28_node, pull_resistor_29_node, pull_resistor_30_node,
       pull_resistor_31_node, pull_resistor_32_node, pull_resistor_33_node, pull_resistor_34_node,
       pull_resistor_35_node, pull_resistor_36_node, pull_resistor_37_node, pull_resistor_38_node,
       pull_resistor_39_node, pull_resistor_40_node, pull_resistor_41_node, pull_resistor_42_node,
       pull_resistor_43_node, pull_resistor_44_node, pull_resistor_45_node, pull_resistor_46_node,
       pull_resistor_47_node, pull_resistor_48_node, pull_resistor_49_node, pull_resistor_50_node,
       pull_resistor_51_node, pull_resistor_52_node, pull_resistor_53_node, pull_resistor_54_node,
       pull_resistor_55_node, pull_resistor_56_node, pull_resistor_57_node, pull_resistor_58_node,
       pull_resistor_59_node, pull_resistor_60_node, pull_resistor_61_node, pull_resistor_62_node,
       pull_resistor_63_node, pull_resistor_64_node;

  adder64bit adder64bit_1 (
    .input1(pull_resistor_1_node), .input2(pull_resistor_2_node), .output1(adder64bit_1_output1));  // open: inflow, overflow
  adder64bit adder64bit_2 (
    .input1(pull_resistor_3_node), .input2(pull_resistor_4_node), .output1(adder64bit_2_output1));  // open: inflow, overflow
  adder64bit adder64bit_3 (
    .input1(pull_resistor_5_node), .input2(pull_resistor_6_node), .output1(adder64bit_3_output1));  // open: inflow, overflow
  adder64bit adder64bit_4 (
    .input1(pull_resistor_7_node), .input2(pull_resistor_8_node), .output1(adder64bit_4_output1));  // open: inflow, overflow
  adder64bit adder64bit_5 (
    .input1(pull_resistor_9_node), .input2(pull_resistor_10_node), .output1(adder64bit_5_output1));  // open: inflow, overflow
  Pull_Resistor pull_resistor_1 (.node(pull_resistor_1_node));
  Pull_Resistor pull_resistor_2 (.node(pull_resistor_2_node));
  assign pull_resistor_1_node = input1[0] ? input2 : 64'bz;  // Controlled_Buffer controlled_buffer_1
  assign pull_resistor_2_node = input1[1] ? {input2[62:0], 1'b0} : 64'bz;  // Controlled_Buffer controlled_buffer_2
  adder64bit adder64bit_6 (
    .input1(pull_resistor_11_node), .input2(pull_resistor_12_node), .output1(adder64bit_6_output1));  // open: inflow, overflow
  Pull_Resistor pull_resistor_3 (.node(pull_resistor_3_node));
  Pull_Resistor pull_resistor_4 (.node(pull_resistor_4_node));
  Pull_Resistor pull_resistor_5 (.node(pull_resistor_5_node));
  assign pull_resistor_3_node = input1[2] ? {input2[61:0], 2'b00} : 64'bz;  // Controlled_Buffer controlled_buffer_3
  assign pull_resistor_4_node = input1[3] ? {input2[60:0], 3'b000} : 64'bz;  // Controlled_Buffer controlled_buffer_4
  assign pull_resistor_5_node = input1[4] ? {input2[59:0], 4'b0000} : 64'bz;  // Controlled_Buffer controlled_buffer_5
  adder64bit adder64bit_7 (
    .input1(pull_resistor_13_node), .input2(pull_resistor_14_node), .output1(adder64bit_7_output1));  // open: inflow, overflow
  Pull_Resistor pull_resistor_6 (.node(pull_resistor_6_node));
  Pull_Resistor pull_resistor_7 (.node(pull_resistor_7_node));
  Pull_Resistor pull_resistor_8 (.node(pull_resistor_8_node));
  assign pull_resistor_6_node = input1[5] ? {input2[58:0], {5{1'b0}}} : 64'bz;  // Controlled_Buffer controlled_buffer_6
  assign pull_resistor_7_node = input1[6] ? {input2[57:0], {6{1'b0}}} : 64'bz;  // Controlled_Buffer controlled_buffer_7
  adder64bit adder64bit_8 (
    .input1(pull_resistor_15_node), .input2(pull_resistor_16_node), .output1(adder64bit_8_output1));  // open: inflow, overflow
  Pull_Resistor pull_resistor_9 (.node(pull_resistor_9_node));
  Pull_Resistor pull_resistor_10 (.node(pull_resistor_10_node));
  assign pull_resistor_8_node = input1[7] ? {input2[56:0], {7{1'b0}}} : 64'bz;  // Controlled_Buffer controlled_buffer_8
  assign pull_resistor_9_node = input1[8] ? {input2[55:0], {8{1'b0}}} : 64'bz;  // Controlled_Buffer controlled_buffer_9
  assign pull_resistor_10_node = input1[9] ? {input2[54:0], {9{1'b0}}} : 64'bz;  // Controlled_Buffer controlled_buffer_10
  adder64bit adder64bit_9 (
    .input1(adder64bit_1_output1), .input2(adder64bit_2_output1), .output1(adder64bit_9_output1));  // open: inflow, overflow
  adder64bit adder64bit_10 (
    .input1(pull_resistor_17_node), .input2(pull_resistor_18_node), .output1(adder64bit_10_output1));  // open: inflow, overflow
  Pull_Resistor pull_resistor_11 (.node(pull_resistor_11_node));
  Pull_Resistor pull_resistor_12 (.node(pull_resistor_12_node));
  Pull_Resistor pull_resistor_13 (.node(pull_resistor_13_node));
  assign pull_resistor_11_node = input1[10] ? {input2[53:0], {10{1'b0}}} : 64'bz;  // Controlled_Buffer controlled_buffer_11
  assign pull_resistor_12_node = input1[11] ? {input2[52:0], {11{1'b0}}} : 64'bz;  // Controlled_Buffer controlled_buffer_12
  assign pull_resistor_13_node = input1[12] ? {input2[51:0], {12{1'b0}}} : 64'bz;  // Controlled_Buffer controlled_buffer_13
  adder64bit adder64bit_11 (
    .input1(adder64bit_3_output1), .input2(adder64bit_4_output1), .output1(adder64bit_11_output1));  // open: inflow, overflow
  adder64bit adder64bit_12 (
    .input1(pull_resistor_19_node), .input2(pull_resistor_20_node), .output1(adder64bit_12_output1));  // open: inflow, overflow
  Pull_Resistor pull_resistor_14 (.node(pull_resistor_14_node));
  Pull_Resistor pull_resistor_15 (.node(pull_resistor_15_node));
  Pull_Resistor pull_resistor_16 (.node(pull_resistor_16_node));
  assign pull_resistor_14_node = input1[13] ? {input2[50:0], {13{1'b0}}} : 64'bz;  // Controlled_Buffer controlled_buffer_14
  assign pull_resistor_15_node = input1[14] ? {input2[49:0], {14{1'b0}}} : 64'bz;  // Controlled_Buffer controlled_buffer_15
  adder64bit adder64bit_13 (
    .input1(adder64bit_5_output1), .input2(adder64bit_6_output1), .output1(adder64bit_13_output1));  // open: inflow, overflow
  adder64bit adder64bit_14 (
    .input1(pull_resistor_21_node), .input2(pull_resistor_22_node), .output1(adder64bit_14_output1));  // open: inflow, overflow
  Pull_Resistor pull_resistor_17 (.node(pull_resistor_17_node));
  Pull_Resistor pull_resistor_18 (.node(pull_resistor_18_node));
  assign pull_resistor_16_node = input1[15] ? {input2[48:0], {15{1'b0}}} : 64'bz;  // Controlled_Buffer controlled_buffer_16
  assign pull_resistor_17_node = input1[16] ? {input2[47:0], {16{1'b0}}} : 64'bz;  // Controlled_Buffer controlled_buffer_17
  assign pull_resistor_18_node = input1[17] ? {input2[46:0], {17{1'b0}}} : 64'bz;  // Controlled_Buffer controlled_buffer_18
  adder64bit adder64bit_15 (
    .input1(adder64bit_7_output1), .input2(adder64bit_8_output1), .output1(adder64bit_15_output1));  // open: inflow, overflow
  Pull_Resistor pull_resistor_19 (.node(pull_resistor_19_node));
  Pull_Resistor pull_resistor_20 (.node(pull_resistor_20_node));
  Pull_Resistor pull_resistor_21 (.node(pull_resistor_21_node));
  assign pull_resistor_19_node = input1[18] ? {input2[45:0], {18{1'b0}}} : 64'bz;  // Controlled_Buffer controlled_buffer_19
  assign pull_resistor_20_node = input1[19] ? {input2[44:0], {19{1'b0}}} : 64'bz;  // Controlled_Buffer controlled_buffer_20
  assign pull_resistor_21_node = input1[20] ? {input2[43:0], {20{1'b0}}} : 64'bz;  // Controlled_Buffer controlled_buffer_21
  adder64bit adder64bit_16 (
    .input1(pull_resistor_23_node), .input2(pull_resistor_24_node), .output1(adder64bit_16_output1));  // open: inflow, overflow
  Pull_Resistor pull_resistor_22 (.node(pull_resistor_22_node));
  Pull_Resistor pull_resistor_23 (.node(pull_resistor_23_node));
  Pull_Resistor pull_resistor_24 (.node(pull_resistor_24_node));
  assign pull_resistor_22_node = input1[21] ? {input2[42:0], {21{1'b0}}} : 64'bz;  // Controlled_Buffer controlled_buffer_22
  assign pull_resistor_23_node = input1[22] ? {input2[41:0], {22{1'b0}}} : 64'bz;  // Controlled_Buffer controlled_buffer_23
  adder64bit adder64bit_17 (
    .input1(adder64bit_9_output1), .input2(adder64bit_11_output1), .output1(adder64bit_17_output1));  // open: inflow, overflow
  adder64bit adder64bit_18 (
    .input1(adder64bit_10_output1), .input2(adder64bit_12_output1), .output1(adder64bit_18_output1));  // open: inflow, overflow
  adder64bit adder64bit_19 (
    .input1(pull_resistor_25_node), .input2(pull_resistor_26_node), .output1(adder64bit_19_output1));  // open: inflow, overflow
  Pull_Resistor pull_resistor_25 (.node(pull_resistor_25_node));
  Pull_Resistor pull_resistor_26 (.node(pull_resistor_26_node));
  assign pull_resistor_24_node = input1[23] ? {input2[40:0], {23{1'b0}}} : 64'bz;  // Controlled_Buffer controlled_buffer_24
  assign pull_resistor_25_node = input1[24] ? {input2[39:0], {24{1'b0}}} : 64'bz;  // Controlled_Buffer controlled_buffer_25
  assign pull_resistor_26_node = input1[25] ? {input2[38:0], {25{1'b0}}} : 64'bz;  // Controlled_Buffer controlled_buffer_26
  adder64bit adder64bit_20 (
    .input1(adder64bit_13_output1), .input2(adder64bit_15_output1), .output1(adder64bit_20_output1));  // open: inflow, overflow
  adder64bit adder64bit_21 (
    .input1(adder64bit_14_output1), .input2(adder64bit_16_output1), .output1(adder64bit_21_output1));  // open: inflow, overflow
  adder64bit adder64bit_22 (
    .input1(pull_resistor_27_node), .input2(pull_resistor_28_node), .output1(adder64bit_22_output1));  // open: inflow, overflow
  Pull_Resistor pull_resistor_27 (.node(pull_resistor_27_node));
  Pull_Resistor pull_resistor_28 (.node(pull_resistor_28_node));
  Pull_Resistor pull_resistor_29 (.node(pull_resistor_29_node));
  assign pull_resistor_27_node = input1[26] ? {input2[37:0], {26{1'b0}}} : 64'bz;  // Controlled_Buffer controlled_buffer_27
  assign pull_resistor_28_node = input1[27] ? {input2[36:0], {27{1'b0}}} : 64'bz;  // Controlled_Buffer controlled_buffer_28
  assign pull_resistor_29_node = input1[28] ? {input2[35:0], {28{1'b0}}} : 64'bz;  // Controlled_Buffer controlled_buffer_29
  adder64bit adder64bit_23 (
    .input1(adder64bit_17_output1), .input2(adder64bit_20_output1), .output1(adder64bit_23_output1));  // open: inflow, overflow
  adder64bit adder64bit_24 (
    .input1(adder64bit_18_output1), .input2(adder64bit_21_output1), .output1(adder64bit_24_output1));  // open: inflow, overflow
  adder64bit adder64bit_25 (
    .input1(adder64bit_19_output1), .input2(adder64bit_22_output1), .output1(adder64bit_25_output1));  // open: inflow, overflow
  adder64bit adder64bit_26 (
    .input1(pull_resistor_29_node), .input2(pull_resistor_30_node), .output1(adder64bit_26_output1));  // open: inflow, overflow
  Pull_Resistor pull_resistor_30 (.node(pull_resistor_30_node));
  Pull_Resistor pull_resistor_31 (.node(pull_resistor_31_node));
  Pull_Resistor pull_resistor_32 (.node(pull_resistor_32_node));
  assign pull_resistor_30_node = input1[29] ? {input2[34:0], {29{1'b0}}} : 64'bz;  // Controlled_Buffer controlled_buffer_30
  assign pull_resistor_31_node = input1[30] ? {input2[33:0], {30{1'b0}}} : 64'bz;  // Controlled_Buffer controlled_buffer_31
  adder64bit adder64bit_27 (
    .input1(adder64bit_28_output1), .input2(adder64bit_33_output1), .output1(output1));  // open: inflow, overflow
  adder64bit adder64bit_28 (
    .input1(adder64bit_23_output1), .input2(adder64bit_29_output1), .output1(adder64bit_28_output1));  // open: inflow, overflow
  adder64bit adder64bit_29 (
    .input1(adder64bit_24_output1), .input2(adder64bit_30_output1), .output1(adder64bit_29_output1));  // open: inflow, overflow
  adder64bit adder64bit_30 (
    .input1(adder64bit_25_output1), .input2(adder64bit_31_output1), .output1(adder64bit_30_output1));  // open: inflow, overflow
  adder64bit adder64bit_31 (
    .input1(adder64bit_26_output1), .input2(adder64bit_32_output1), .output1(adder64bit_31_output1));  // open: inflow, overflow
  adder64bit adder64bit_32 (
    .input1(pull_resistor_31_node), .input2(pull_resistor_32_node), .output1(adder64bit_32_output1));  // open: inflow, overflow
  Pull_Resistor pull_resistor_33 (.node(pull_resistor_33_node));
  Pull_Resistor pull_resistor_34 (.node(pull_resistor_34_node));
  assign pull_resistor_32_node = input1[31] ? {input2[32:0], {31{1'b0}}} : 64'bz;  // Controlled_Buffer controlled_buffer_32
  assign pull_resistor_33_node = input1[32] ? {input2[31:0], {32{1'b0}}} : 64'bz;  // Controlled_Buffer controlled_buffer_33
  assign pull_resistor_34_node = input1[33] ? {input2[30:0], {33{1'b0}}} : 64'bz;  // Controlled_Buffer controlled_buffer_34
  adder64bit adder64bit_33 (
    .input1(adder64bit_34_output1), .input2(adder64bit_38_output1), .output1(adder64bit_33_output1));  // open: inflow, overflow
  adder64bit adder64bit_34 (
    .input1(adder64bit_35_output1), .input2(adder64bit_39_output1), .output1(adder64bit_34_output1));  // open: inflow, overflow
  adder64bit adder64bit_35 (
    .input1(adder64bit_36_output1), .input2(adder64bit_40_output1), .output1(adder64bit_35_output1));  // open: inflow, overflow
  adder64bit adder64bit_36 (
    .input1(adder64bit_37_output1), .input2(adder64bit_41_output1), .output1(adder64bit_36_output1));  // open: inflow, overflow
  adder64bit adder64bit_37 (
    .input1(pull_resistor_33_node), .input2(pull_resistor_34_node), .output1(adder64bit_37_output1));  // open: inflow, overflow
  Pull_Resistor pull_resistor_35 (.node(pull_resistor_35_node));
  Pull_Resistor pull_resistor_36 (.node(pull_resistor_36_node));
  Pull_Resistor pull_resistor_37 (.node(pull_resistor_37_node));
  assign pull_resistor_35_node = input1[34] ? {input2[29:0], {34{1'b0}}} : 64'bz;  // Controlled_Buffer controlled_buffer_35
  assign pull_resistor_36_node = input1[35] ? {input2[28:0], {35{1'b0}}} : 64'bz;  // Controlled_Buffer controlled_buffer_36
  assign pull_resistor_37_node = input1[36] ? {input2[27:0], {36{1'b0}}} : 64'bz;  // Controlled_Buffer controlled_buffer_37
  adder64bit adder64bit_38 (
    .input1(adder64bit_42_output1), .input2(adder64bit_45_output1), .output1(adder64bit_38_output1));  // open: inflow, overflow
  adder64bit adder64bit_39 (
    .input1(adder64bit_43_output1), .input2(adder64bit_46_output1), .output1(adder64bit_39_output1));  // open: inflow, overflow
  adder64bit adder64bit_40 (
    .input1(adder64bit_44_output1), .input2(adder64bit_47_output1), .output1(adder64bit_40_output1));  // open: inflow, overflow
  adder64bit adder64bit_41 (
    .input1(pull_resistor_35_node), .input2(pull_resistor_36_node), .output1(adder64bit_41_output1));  // open: inflow, overflow
  Pull_Resistor pull_resistor_38 (.node(pull_resistor_38_node));
  Pull_Resistor pull_resistor_39 (.node(pull_resistor_39_node));
  Pull_Resistor pull_resistor_40 (.node(pull_resistor_40_node));
  assign pull_resistor_38_node = input1[37] ? {input2[26:0], {37{1'b0}}} : 64'bz;  // Controlled_Buffer controlled_buffer_38
  assign pull_resistor_39_node = input1[38] ? {input2[25:0], {38{1'b0}}} : 64'bz;  // Controlled_Buffer controlled_buffer_39
  adder64bit adder64bit_42 (
    .input1(adder64bit_48_output1), .input2(adder64bit_50_output1), .output1(adder64bit_42_output1));  // open: inflow, overflow
  adder64bit adder64bit_43 (
    .input1(adder64bit_49_output1), .input2(adder64bit_51_output1), .output1(adder64bit_43_output1));  // open: inflow, overflow
  adder64bit adder64bit_44 (
    .input1(pull_resistor_37_node), .input2(pull_resistor_38_node), .output1(adder64bit_44_output1));  // open: inflow, overflow
  Pull_Resistor pull_resistor_41 (.node(pull_resistor_41_node));
  Pull_Resistor pull_resistor_42 (.node(pull_resistor_42_node));
  assign pull_resistor_40_node = input1[39] ? {input2[24:0], {39{1'b0}}} : 64'bz;  // Controlled_Buffer controlled_buffer_40
  assign pull_resistor_41_node = input1[40] ? {input2[23:0], {40{1'b0}}} : 64'bz;  // Controlled_Buffer controlled_buffer_41
  assign pull_resistor_42_node = input1[41] ? {input2[22:0], {41{1'b0}}} : 64'bz;  // Controlled_Buffer controlled_buffer_42
  adder64bit adder64bit_45 (
    .input1(adder64bit_52_output1), .input2(adder64bit_54_output1), .output1(adder64bit_45_output1));  // open: inflow, overflow
  adder64bit adder64bit_46 (
    .input1(adder64bit_53_output1), .input2(adder64bit_55_output1), .output1(adder64bit_46_output1));  // open: inflow, overflow
  Pull_Resistor pull_resistor_43 (.node(pull_resistor_43_node));
  Pull_Resistor pull_resistor_44 (.node(pull_resistor_44_node));
  Pull_Resistor pull_resistor_45 (.node(pull_resistor_45_node));
  assign pull_resistor_43_node = input1[42] ? {input2[21:0], {42{1'b0}}} : 64'bz;  // Controlled_Buffer controlled_buffer_43
  assign pull_resistor_44_node = input1[43] ? {input2[20:0], {43{1'b0}}} : 64'bz;  // Controlled_Buffer controlled_buffer_44
  assign pull_resistor_45_node = input1[44] ? {input2[19:0], {44{1'b0}}} : 64'bz;  // Controlled_Buffer controlled_buffer_45
  adder64bit adder64bit_47 (
    .input1(pull_resistor_39_node), .input2(pull_resistor_40_node), .output1(adder64bit_47_output1));  // open: inflow, overflow
  Pull_Resistor pull_resistor_46 (.node(pull_resistor_46_node));
  Pull_Resistor pull_resistor_47 (.node(pull_resistor_47_node));
  Pull_Resistor pull_resistor_48 (.node(pull_resistor_48_node));
  assign pull_resistor_46_node = input1[45] ? {input2[18:0], {45{1'b0}}} : 64'bz;  // Controlled_Buffer controlled_buffer_46
  assign pull_resistor_47_node = input1[46] ? {input2[17:0], {46{1'b0}}} : 64'bz;  // Controlled_Buffer controlled_buffer_47
  adder64bit adder64bit_48 (
    .input1(adder64bit_56_output1), .input2(adder64bit_57_output1), .output1(adder64bit_48_output1));  // open: inflow, overflow
  adder64bit adder64bit_49 (
    .input1(pull_resistor_41_node), .input2(pull_resistor_42_node), .output1(adder64bit_49_output1));  // open: inflow, overflow
  Pull_Resistor pull_resistor_49 (.node(pull_resistor_49_node));
  Pull_Resistor pull_resistor_50 (.node(pull_resistor_50_node));
  assign pull_resistor_48_node = input1[47] ? {input2[16:0], {47{1'b0}}} : 64'bz;  // Controlled_Buffer controlled_buffer_48
  assign pull_resistor_49_node = input1[48] ? {input2[15:0], {48{1'b0}}} : 64'bz;  // Controlled_Buffer controlled_buffer_49
  assign pull_resistor_50_node = input1[49] ? {input2[14:0], {49{1'b0}}} : 64'bz;  // Controlled_Buffer controlled_buffer_50
  adder64bit adder64bit_50 (
    .input1(adder64bit_58_output1), .input2(adder64bit_59_output1), .output1(adder64bit_50_output1));  // open: inflow, overflow
  adder64bit adder64bit_51 (
    .input1(pull_resistor_43_node), .input2(pull_resistor_44_node), .output1(adder64bit_51_output1));  // open: inflow, overflow
  Pull_Resistor pull_resistor_51 (.node(pull_resistor_51_node));
  Pull_Resistor pull_resistor_52 (.node(pull_resistor_52_node));
  Pull_Resistor pull_resistor_53 (.node(pull_resistor_53_node));
  assign pull_resistor_51_node = input1[50] ? {input2[13:0], {50{1'b0}}} : 64'bz;  // Controlled_Buffer controlled_buffer_51
  assign pull_resistor_52_node = input1[51] ? {input2[12:0], {51{1'b0}}} : 64'bz;  // Controlled_Buffer controlled_buffer_52
  assign pull_resistor_53_node = input1[52] ? {input2[11:0], {52{1'b0}}} : 64'bz;  // Controlled_Buffer controlled_buffer_53
  adder64bit adder64bit_52 (
    .input1(adder64bit_60_output1), .input2(adder64bit_61_output1), .output1(adder64bit_52_output1));  // open: inflow, overflow
  adder64bit adder64bit_53 (
    .input1(pull_resistor_45_node), .input2(pull_resistor_46_node), .output1(adder64bit_53_output1));  // open: inflow, overflow
  Pull_Resistor pull_resistor_54 (.node(pull_resistor_54_node));
  Pull_Resistor pull_resistor_55 (.node(pull_resistor_55_node));
  Pull_Resistor pull_resistor_56 (.node(pull_resistor_56_node));
  assign pull_resistor_54_node = input1[53] ? {input2[10:0], {53{1'b0}}} : 64'bz;  // Controlled_Buffer controlled_buffer_54
  assign pull_resistor_55_node = input1[54] ? {input2[9:0], {54{1'b0}}} : 64'bz;  // Controlled_Buffer controlled_buffer_55
  adder64bit adder64bit_54 (
    .input1(adder64bit_62_output1), .input2(adder64bit_63_output1), .output1(adder64bit_54_output1));  // open: inflow, overflow
  adder64bit adder64bit_55 (
    .input1(pull_resistor_47_node), .input2(pull_resistor_48_node), .output1(adder64bit_55_output1));  // open: inflow, overflow
  Pull_Resistor pull_resistor_57 (.node(pull_resistor_57_node));
  Pull_Resistor pull_resistor_58 (.node(pull_resistor_58_node));
  assign pull_resistor_56_node = input1[55] ? {input2[8:0], {55{1'b0}}} : 64'bz;  // Controlled_Buffer controlled_buffer_56
  assign pull_resistor_57_node = input1[56] ? {input2[7:0], {56{1'b0}}} : 64'bz;  // Controlled_Buffer controlled_buffer_57
  assign pull_resistor_58_node = input1[57] ? {input2[6:0], {57{1'b0}}} : 64'bz;  // Controlled_Buffer controlled_buffer_58
  adder64bit adder64bit_56 (
    .input1(pull_resistor_49_node), .input2(pull_resistor_50_node), .output1(adder64bit_56_output1));  // open: inflow, overflow
  Pull_Resistor pull_resistor_59 (.node(pull_resistor_59_node));
  Pull_Resistor pull_resistor_60 (.node(pull_resistor_60_node));
  Pull_Resistor pull_resistor_61 (.node(pull_resistor_61_node));
  assign pull_resistor_59_node = input1[58] ? {input2[5:0], {58{1'b0}}} : 64'bz;  // Controlled_Buffer controlled_buffer_59
  assign pull_resistor_60_node = input1[59] ? {input2[4:0], {59{1'b0}}} : 64'bz;  // Controlled_Buffer controlled_buffer_60
  assign pull_resistor_61_node = input1[60] ? {input2[3:0], {60{1'b0}}} : 64'bz;  // Controlled_Buffer controlled_buffer_61
  adder64bit adder64bit_57 (
    .input1(pull_resistor_51_node), .input2(pull_resistor_52_node), .output1(adder64bit_57_output1));  // open: inflow, overflow
  Pull_Resistor pull_resistor_62 (.node(pull_resistor_62_node));
  Pull_Resistor pull_resistor_63 (.node(pull_resistor_63_node));
  Pull_Resistor pull_resistor_64 (.node(pull_resistor_64_node));
  assign pull_resistor_62_node = input1[61] ? {input2[2:0], {61{1'b0}}} : 64'bz;  // Controlled_Buffer controlled_buffer_62
  assign pull_resistor_63_node = input1[62] ? {input2[1:0], {62{1'b0}}} : 64'bz;  // Controlled_Buffer controlled_buffer_63
  adder64bit adder64bit_58 (
    .input1(pull_resistor_53_node), .input2(pull_resistor_54_node), .output1(adder64bit_58_output1));  // open: inflow, overflow
  assign pull_resistor_64_node = input1[63] ? {input2[0], {63{1'b0}}} : 64'bz;  // Controlled_Buffer controlled_buffer_64
  adder64bit adder64bit_59 (
    .input1(pull_resistor_55_node), .input2(pull_resistor_56_node), .output1(adder64bit_59_output1));  // open: inflow, overflow
  adder64bit adder64bit_60 (
    .input1(pull_resistor_57_node), .input2(pull_resistor_58_node), .output1(adder64bit_60_output1));  // open: inflow, overflow
  adder64bit adder64bit_61 (
    .input1(pull_resistor_59_node), .input2(pull_resistor_60_node), .output1(adder64bit_61_output1));  // open: inflow, overflow
  adder64bit adder64bit_62 (
    .input1(pull_resistor_61_node), .input2(pull_resistor_62_node), .output1(adder64bit_62_output1));  // open: inflow, overflow
  adder64bit adder64bit_63 (
    .input1(pull_resistor_63_node), .input2(pull_resistor_64_node), .output1(adder64bit_63_output1));  // open: inflow, overflow

  // Notes on the sheet:
  //   input1: initial=0x123456789abcdef
  //   input2: initial=0x123456789abcdef
endmodule

module adder128bit (
  input  inflow,
  input  [63:0] input1a,
  input  [63:0] input1b,
  input  [63:0] input2a,
  input  [63:0] input2b,
  output overflow,
  output [63:0] output1a,
  output [63:0] output1b
);

  wire adder64bit_1_overflow;

  adder64bit adder64bit_1 (
    .inflow(inflow), .input1(input1a), .input2(input2a), .overflow(adder64bit_1_overflow), .output1(output1a));
  adder64bit adder64bit_2 (
    .inflow(adder64bit_1_overflow), .input1(input1b), .input2(input2b), .overflow(overflow),
    .output1(output1b));
endmodule

module negate128bit (
  input  [63:0] input1a,
  input  [63:0] input1b,
  output [63:0] output1a,
  output [63:0] output1b
);

  wire [63:0] not_1_out, not_2_out;

  assign not_1_out = ~input1a;  // NOT_Gate not_1, 64 bits wide
  assign not_2_out = ~input1b;  // NOT_Gate not_2, 64 bits wide
  adder128bit adder128bit_1 (
    .input1a(64'h1), .input2a(not_1_out), .input2b(not_2_out), .output1a(output1a), .output1b(output1b));  // open: inflow, input1b, overflow
endmodule

module subtractor128bit (
  input  inborrow,
  input  [63:0] input1a,
  input  [63:0] input1b,
  input  [63:0] input2a,
  input  [63:0] input2b,
  output borrow,
  output [63:0] output1a,
  output [63:0] output1b
);

  wire subtractor64bit_1_borrow;

  subtractor64bit subtractor64bit_1 (
    .inborrow(inborrow), .input1(input1a), .input2(input2a), .borrow(subtractor64bit_1_borrow),
    .output1(output1a));
  subtractor64bit subtractor64bit_2 (
    .inborrow(subtractor64bit_1_borrow), .input1(input1b), .input2(input2b), .borrow(borrow),
    .output1(output1b));
endmodule
