// Logisim project microfpgamux.circ as structural Verilog: 2 circuits, main circuit muxcore
module muxcore (
);

  muxreg muxreg_1 ();  // open: IN0, IN1, IN2, IN3, IN4, IN5, IN6, IN7, IN8, IN9, IN10, IN11, IN12, IN13, IN14, IN15, A0, A1, A2, A3, A4, A5, A6, A7, A8, A9, A10, A11, A12, A13, A14, A15, LE0, LE1, LE2, LE3, LE4, LE5, LE6, LE7, LE8, LE9, LE10, LE11, LE12, LE13, LE14, LE15, DA0, DB0, DA1, DB1, DA2, DB2, DA3, DB3, DA4, DB4, DA5, DB5, DA6, DB6, DA7, DB7, DA8, DB8, DA9, DB9, DA10, DB10, DA11, DB11, DA12, DB12, DA13, DB13, DA14, DB14, DA15, DB15, OUTA0, OUTB0, OUTA1, OUTB1, OUTA2, OUTB2, OUTA3, OUTB3, OUTA4, OUTB4, OUTA5, OUTB5, OUTA6, OUTB6, OUTA7, OUTB7, OUTA8, OUTB8, OUTA9, OUTB9, OUTA10, OUTB10, OUTA11, OUTB11, OUTA12, OUTB12, OUTA13, OUTB13, OUTA14, OUTB14, OUTA15, OUTB15
endmodule

module muxreg (
  input  [63:0] IN0,
  input  [63:0] IN1,
  input  [63:0] IN2,
  input  [63:0] IN3,
  input  [63:0] IN4,
  input  [63:0] IN5,
  input  [63:0] IN6,
  input  [63:0] IN7,
  input  [63:0] IN8,
  input  [63:0] IN9,
  input  [63:0] IN10,
  input  [63:0] IN11,
  input  [63:0] IN12,
  input  [63:0] IN13,
  input  [63:0] IN14,
  input  [63:0] IN15,
  input  [3:0] A0,
  input  [3:0] A1,
  input  [3:0] A2,
  input  [3:0] A3,
  input  [3:0] A4,
  input  [3:0] A5,
  input  [3:0] A6,
  input  [3:0] A7,
  input  [3:0] A8,
  input  [3:0] A9,
  input  [3:0] A10,
  input  [3:0] A11,
  input  [3:0] A12,
  input  [3:0] A13,
  input  [3:0] A14,
  input  [3:0] A15,
  input  LE0,
  input  LE1,
  input  LE2,
  input  LE3,
  input  LE4,
  input  LE5,
  input  LE6,
  input  LE7,
  input  LE8,
  input  LE9,
  input  LE10,
  input  LE11,
  input  LE12,
  input  LE13,
  input  LE14,
  input  LE15,
  input  [3:0] DA0,
  input  [3:0] DB0,
  input  [3:0] DA1,
  input  [3:0] DB1,
  input  [3:0] DA2,
  input  [3:0] DB2,
  input  [3:0] DA3,
  input  [3:0] DB3,
  input  [3:0] DA4,
  input  [3:0] DB4,
  input  [3:0] DA5,
  input  [3:0] DB5,
  input  [3:0] DA6,
  input  [3:0] DB6,
  input  [3:0] DA7,
  input  [3:0] DB7,
  input  [3:0] DA8,
  input  [3:0] DB8,
  input  [3:0] DA9,
  input  [3:0] DB9,
  input  [3:0] DA10,
  input  [3:0] DB10,
  input  [3:0] DA11,
  input  [3:0] DB11,
  input  [3:0] DA12,
  input  [3:0] DB12,
  input  [3:0] DA13,
  input  [3:0] DB13,
  input  [3:0] DA14,
  input  [3:0] DB14,
  input  [3:0] DA15,
  input  [3:0] DB15,
  output [63:0] OUTA0,
  output [63:0] OUTB0,
  output [63:0] OUTA1,
  output [63:0] OUTB1,
  output [63:0] OUTA2,
  output [63:0] OUTB2,
  output [63:0] OUTA3,
  output [63:0] OUTB3,
  output [63:0] OUTA4,
  output [63:0] OUTB4,
  output [63:0] OUTA5,
  output [63:0] OUTB5,
  output [63:0] OUTA6,
  output [63:0] OUTB6,
  output [63:0] OUTA7,
  output [63:0] OUTB7,
  output [63:0] OUTA8,
  output [63:0] OUTB8,
  output [63:0] OUTA9,
  output [63:0] OUTB9,
  output [63:0] OUTA10,
  output [63:0] OUTB10,
  output [63:0] OUTA11,
  output [63:0] OUTB11,
  output [63:0] OUTA12,
  output [63:0] OUTB12,
  output [63:0] OUTA13,
  output [63:0] OUTB13,
  output [63:0] OUTA14,
  output [63:0] OUTB14,
  output [63:0] OUTA15,
  output [63:0] OUTB15
);

  wire clock_1_out, clock_2_out, clock_3_out, clock_4_out, clock_5_out, clock_6_out, clock_7_out,
       clock_8_out, clock_9_out, clock_10_out, clock_11_out, clock_12_out, clock_13_out, clock_14_out,
       clock_15_out, clock_16_out;
  wire [63:0] multiplexer_1_out, multiplexer_4_out, multiplexer_7_out, multiplexer_10_out,
       multiplexer_13_out, multiplexer_16_out, multiplexer_21_out, multiplexer_22_out, multiplexer_27_out,
       multiplexer_30_out, multiplexer_33_out, multiplexer_36_out, multiplexer_39_out, multiplexer_42_out,
       multiplexer_45_out, multiplexer_48_out, OUT0, OUT1, OUT2, OUT3, OUT4, OUT5, OUT6, OUT7, OUT8, OUT9,
       OUT10, OUT11, OUT12, OUT13, OUT14, OUT15;

  Multiplexer #(.select(4), .width(64)) multiplexer_1 (
    .in0(IN0), .in1(IN1), .in2(IN2), .in3(IN3), .in4(IN4), .in5(IN5), .in6(IN6), .in7(IN7), .in8(IN8),
    .in9(IN9), .in10(IN10), .in11(IN11), .in12(IN12), .in13(IN13), .in14(IN14), .in15(IN15),
    .out(multiplexer_1_out), .sel(A0));
  Register #(.width(64)) reg0 (.D(multiplexer_1_out), .en(LE0), .clk(clock_1_out), .Q(OUT0));  // open: clr
  Clock clock_1 (.out(clock_1_out));
  Multiplexer #(.select(4), .width(64)) multiplexer_2 (
    .in0(OUT0), .in1(OUT1), .in2(OUT2), .in3(OUT3), .in4(OUT4), .in5(OUT5), .in6(OUT6), .in7(OUT7),
    .in8(OUT8), .in9(OUT9), .in10(OUT10), .in11(OUT11), .in12(OUT12), .in13(OUT13), .in14(OUT14),
    .in15(OUT15), .out(OUTA0), .sel(DA0));
  Multiplexer #(.select(4), .width(64)) multiplexer_3 (
    .in0(OUT0), .in1(OUT1), .in2(OUT2), .in3(OUT3), .in4(OUT4), .in5(OUT5), .in6(OUT6), .in7(OUT7),
    .in8(OUT8), .in9(OUT9), .in10(OUT10), .in11(OUT11), .in12(OUT12), .in13(OUT13), .in14(OUT14),
    .in15(OUT15), .out(OUTA8), .sel(DA8));
  Multiplexer #(.select(4), .width(64)) multiplexer_4 (
    .in0(IN0), .in1(IN1), .in2(IN2), .in3(IN3), .in4(IN4), .in5(IN5), .in6(IN6), .in7(IN7), .in8(IN8),
    .in9(IN9), .in10(IN10), .in11(IN11), .in12(IN12), .in13(IN13), .in14(IN14), .in15(IN15),
    .out(multiplexer_4_out), .sel(A1));
  Register #(.width(64)) reg1 (.D(multiplexer_4_out), .en(LE1), .clk(clock_2_out), .Q(OUT1));  // open: clr
  Clock clock_2 (.out(clock_2_out));
  Multiplexer #(.select(4), .width(64)) multiplexer_5 (
    .in0(OUT0), .in1(OUT1), .in2(OUT2), .in3(OUT3), .in4(OUT4), .in5(OUT5), .in6(OUT6), .in7(OUT7),
    .in8(OUT8), .in9(OUT9), .in10(OUT10), .in11(OUT11), .in12(OUT12), .in13(OUT13), .in14(OUT14),
    .in15(OUT15), .out(OUTB0), .sel(DB0));
  Multiplexer #(.select(4), .width(64)) multiplexer_6 (
    .in0(OUT0), .in1(OUT1), .in2(OUT2), .in3(OUT3), .in4(OUT4), .in5(OUT5), .in6(OUT6), .in7(OUT7),
    .in8(OUT8), .in9(OUT9), .in10(OUT10), .in11(OUT11), .in12(OUT12), .in13(OUT13), .in14(OUT14),
    .in15(OUT15), .out(OUTB8), .sel(DB8));
  Multiplexer #(.select(4), .width(64)) multiplexer_7 (
    .in0(IN0), .in1(IN1), .in2(IN2), .in3(IN3), .in4(IN4), .in5(IN5), .in6(IN6), .in7(IN7), .in8(IN8),
    .in9(IN9), .in10(IN10), .in11(IN11), .in12(IN12), .in13(IN13), .in14(IN14), .in15(IN15),
    .out(multiplexer_7_out), .sel(A2));
  Register #(.width(64)) reg2 (.D(multiplexer_7_out), .en(LE2), .clk(clock_3_out), .Q(OUT2));  // open: clr
  Clock clock_3 (.out(clock_3_out));
  Multiplexer #(.select(4), .width(64)) multiplexer_8 (
    .in0(OUT0), .in1(OUT1), .in2(OUT2), .in3(OUT3), .in4(OUT4), .in5(OUT5), .in6(OUT6), .in7(OUT7),
    .in8(OUT8), .in9(OUT9), .in10(OUT10), .in11(OUT11), .in12(OUT12), .in13(OUT13), .in14(OUT14),
    .in15(OUT15), .out(OUTA1), .sel(DA1));
  Multiplexer #(.select(4), .width(64)) multiplexer_9 (
    .in0(OUT0), .in1(OUT1), .in2(OUT2), .in3(OUT3), .in4(OUT4), .in5(OUT5), .in6(OUT6), .in7(OUT7),
    .in8(OUT8), .in9(OUT9), .in10(OUT10), .in11(OUT11), .in12(OUT12), .in13(OUT13), .in14(OUT14),
    .in15(OUT15), .out(OUTA9), .sel(DA9));
  Multiplexer #(.select(4), .width(64)) multiplexer_10 (
    .in0(IN0), .in1(IN1), .in2(IN2), .in3(IN3), .in4(IN4), .in5(IN5), .in6(IN6), .in7(IN7), .in8(IN8),
    .in9(IN9), .in10(IN10), .in11(IN11), .in12(IN12), .in13(IN13), .in14(IN14), .in15(IN15),
    .out(multiplexer_10_out), .sel(A3));
  Register #(.width(64)) reg3 (.D(multiplexer_10_out), .en(LE3), .clk(clock_4_out), .Q(OUT3));  // open: clr
  Clock clock_4 (.out(clock_4_out));
  Multiplexer #(.select(4), .width(64)) multiplexer_11 (
    .in0(OUT0), .in1(OUT1), .in2(OUT2), .in3(OUT3), .in4(OUT4), .in5(OUT5), .in6(OUT6), .in7(OUT7),
    .in8(OUT8), .in9(OUT9), .in10(OUT10), .in11(OUT11), .in12(OUT12), .in13(OUT13), .in14(OUT14),
    .in15(OUT15), .out(OUTB1), .sel(DB1));
  Multiplexer #(.select(4), .width(64)) multiplexer_12 (
    .in0(OUT0), .in1(OUT1), .in2(OUT2), .in3(OUT3), .in4(OUT4), .in5(OUT5), .in6(OUT6), .in7(OUT7),
    .in8(OUT8), .in9(OUT9), .in10(OUT10), .in11(OUT11), .in12(OUT12), .in13(OUT13), .in14(OUT14),
    .in15(OUT15), .out(OUTB9), .sel(DB9));
  Multiplexer #(.select(4), .width(64)) multiplexer_13 (
    .in0(IN0), .in1(IN1), .in2(IN2), .in3(IN3), .in4(IN4), .in5(IN5), .in6(IN6), .in7(IN7), .in8(IN8),
    .in9(IN9), .in10(IN10), .in11(IN11), .in12(IN12), .in13(IN13), .in14(IN14), .in15(IN15),
    .out(multiplexer_13_out), .sel(A4));
  Register #(.width(64)) reg4 (.D(multiplexer_13_out), .en(LE4), .clk(clock_5_out), .Q(OUT4));  // open: clr
  Clock clock_5 (.out(clock_5_out));
  Multiplexer #(.select(4), .width(64)) multiplexer_14 (
    .in0(OUT0), .in1(OUT1), .in2(OUT2), .in3(OUT3), .in4(OUT4), .in5(OUT5), .in6(OUT6), .in7(OUT7),
    .in8(OUT8), .in9(OUT9), .in10(OUT10), .in11(OUT11), .in12(OUT12), .in13(OUT13), .in14(OUT14),
    .in15(OUT15), .out(OUTA2), .sel(DA2));
  Multiplexer #(.select(4), .width(64)) multiplexer_15 (
    .in0(OUT0), .in1(OUT1), .in2(OUT2), .in3(OUT3), .in4(OUT4), .in5(OUT5), .in6(OUT6), .in7(OUT7),
    .in8(OUT8), .in9(OUT9), .in10(OUT10), .in11(OUT11), .in12(OUT12), .in13(OUT13), .in14(OUT14),
    .in15(OUT15), .out(OUTA10), .sel(DA10));
  Multiplexer #(.select(4), .width(64)) multiplexer_16 (
    .in0(IN0), .in1(IN1), .in2(IN2), .in3(IN3), .in4(IN4), .in5(IN5), .in6(IN6), .in7(IN7), .in8(IN8),
    .in9(IN9), .in10(IN10), .in11(IN11), .in12(IN12), .in13(IN13), .in14(IN14), .in15(IN15),
    .out(multiplexer_16_out), .sel(A5));
  Register #(.width(64)) reg5 (.D(multiplexer_16_out), .en(LE5), .clk(clock_6_out), .Q(OUT5));  // open: clr
  Clock clock_6 (.out(clock_6_out));
  Multiplexer #(.select(4), .width(64)) multiplexer_17 (
    .in0(OUT0), .in1(OUT1), .in2(OUT2), .in3(OUT3), .in4(OUT4), .in5(OUT5), .in6(OUT6), .in7(OUT7),
    .in8(OUT8), .in9(OUT9), .in10(OUT10), .in11(OUT11), .in12(OUT12), .in13(OUT13), .in14(OUT14),
    .in15(OUT15), .out(OUTB2), .sel(DB2));
  Multiplexer #(.select(4), .width(64)) multiplexer_18 (
    .in0(OUT0), .in1(OUT1), .in2(OUT2), .in3(OUT3), .in4(OUT4), .in5(OUT5), .in6(OUT6), .in7(OUT7),
    .in8(OUT8), .in9(OUT9), .in10(OUT10), .in11(OUT11), .in12(OUT12), .in13(OUT13), .in14(OUT14),
    .in15(OUT15), .out(OUTB10), .sel(DB10));
  Multiplexer #(.select(4), .width(64)) multiplexer_19 (
    .in0(OUT0), .in1(OUT1), .in2(OUT2), .in3(OUT3), .in4(OUT4), .in5(OUT5), .in6(OUT6), .in7(OUT7),
    .in8(OUT8), .in9(OUT9), .in10(OUT10), .in11(OUT11), .in12(OUT12), .in13(OUT13), .in14(OUT14),
    .in15(OUT15), .out(OUTA3), .sel(DA3));
  Multiplexer #(.select(4), .width(64)) multiplexer_20 (
    .in0(OUT0), .in1(OUT1), .in2(OUT2), .in3(OUT3), .in4(OUT4), .in5(OUT5), .in6(OUT6), .in7(OUT7),
    .in8(OUT8), .in9(OUT9), .in10(OUT10), .in11(OUT11), .in12(OUT12), .in13(OUT13), .in14(OUT14),
    .in15(OUT15), .out(OUTA11), .sel(DA11));
  Multiplexer #(.select(4), .width(64)) multiplexer_21 (
    .in0(IN0), .in1(IN1), .in2(IN2), .in3(IN3), .in4(IN4), .in5(IN5), .in6(IN6), .in7(IN7), .in8(IN8),
    .in9(IN9), .in10(IN10), .in11(IN11), .in12(IN12), .in13(IN13), .in14(IN14), .in15(IN15),
    .out(multiplexer_21_out), .sel(A6));
  Register #(.width(64)) reg6 (.D(multiplexer_21_out), .en(LE6), .clk(clock_7_out), .Q(OUT6));  // open: clr
  Clock clock_7 (.out(clock_7_out));
  Multiplexer #(.select(4), .width(64)) multiplexer_22 (
    .in0(IN0), .in1(IN1), .in2(IN2), .in3(IN3), .in4(IN4), .in5(IN5), .in6(IN6), .in7(IN7), .in8(IN8),
    .in9(IN9), .in10(IN10), .in11(IN11), .in12(IN12), .in13(IN13), .in14(IN14), .in15(IN15),
    .out(multiplexer_22_out), .sel(A7));
  Register #(.width(64)) reg7 (.D(multiplexer_22_out), .en(LE7), .clk(clock_8_out), .Q(OUT7));  // open: clr
  Clock clock_8 (.out(clock_8_out));
  Multiplexer #(.select(4), .width(64)) multiplexer_23 (
    .in0(OUT0), .in1(OUT1), .in2(OUT2), .in3(OUT3), .in4(OUT4), .in5(OUT5), .in6(OUT6), .in7(OUT7),
    .in8(OUT8), .in9(OUT9), .in10(OUT10), .in11(OUT11), .in12(OUT12), .in13(OUT13), .in14(OUT14),
    .in15(OUT15), .out(OUTB3), .sel(DB3));
  Multiplexer #(.select(4), .width(64)) multiplexer_24 (
    .in0(OUT0), .in1(OUT1), .in2(OUT2), .in3(OUT3), .in4(OUT4), .in5(OUT5), .in6(OUT6), .in7(OUT7),
    .in8(OUT8), .in9(OUT9), .in10(OUT10), .in11(OUT11), .in12(OUT12), .in13(OUT13), .in14(OUT14),
    .in15(OUT15), .out(OUTB11), .sel(DB11));
  Multiplexer #(.select(4), .width(64)) multiplexer_25 (
    .in0(OUT0), .in1(OUT1), .in2(OUT2), .in3(OUT3), .in4(OUT4), .in5(OUT5), .in6(OUT6), .in7(OUT7),
    .in8(OUT8), .in9(OUT9), .in10(OUT10), .in11(OUT11), .in12(OUT12), .in13(OUT13), .in14(OUT14),
    .in15(OUT15), .out(OUTA4), .sel(DA4));
  Multiplexer #(.select(4), .width(64)) multiplexer_26 (
    .in0(OUT0), .in1(OUT1), .in2(OUT2), .in3(OUT3), .in4(OUT4), .in5(OUT5), .in6(OUT6), .in7(OUT7),
    .in8(OUT8), .in9(OUT9), .in10(OUT10), .in11(OUT11), .in12(OUT12), .in13(OUT13), .in14(OUT14),
    .in15(OUT15), .out(OUTA12), .sel(DA12));
  Multiplexer #(.select(4), .width(64)) multiplexer_27 (
    .in0(IN0), .in1(IN1), .in2(IN2), .in3(IN3), .in4(IN4), .in5(IN5), .in6(IN6), .in7(IN7), .in8(IN8),
    .in9(IN9), .in10(IN10), .in11(IN11), .in12(IN12), .in13(IN13), .in14(IN14), .in15(IN15),
    .out(multiplexer_27_out), .sel(A8));
  Register #(.width(64)) reg8 (.D(multiplexer_27_out), .en(LE8), .clk(clock_9_out), .Q(OUT8));  // open: clr
  Clock clock_9 (.out(clock_9_out));
  Multiplexer #(.select(4), .width(64)) multiplexer_28 (
    .in0(OUT0), .in1(OUT1), .in2(OUT2), .in3(OUT3), .in4(OUT4), .in5(OUT5), .in6(OUT6), .in7(OUT7),
    .in8(OUT8), .in9(OUT9), .in10(OUT10), .in11(OUT11), .in12(OUT12), .in13(OUT13), .in14(OUT14),
    .in15(OUT15), .out(OUTB4), .sel(DB4));
  Multiplexer #(.select(4), .width(64)) multiplexer_29 (
    .in0(OUT0), .in1(OUT1), .in2(OUT2), .in3(OUT3), .in4(OUT4), .in5(OUT5), .in6(OUT6), .in7(OUT7),
    .in8(OUT8), .in9(OUT9), .in10(OUT10), .in11(OUT11), .in12(OUT12), .in13(OUT13), .in14(OUT14),
    .in15(OUT15), .out(OUTB12), .sel(DB12));
  Multiplexer #(.select(4), .width(64)) multiplexer_30 (
    .in0(IN0), .in1(IN1), .in2(IN2), .in3(IN3), .in4(IN4), .in5(IN5), .in6(IN6), .in7(IN7), .in8(IN8),
    .in9(IN9), .in10(IN10), .in11(IN11), .in12(IN12), .in13(IN13), .in14(IN14), .in15(IN15),
    .out(multiplexer_30_out), .sel(A9));
  Register #(.width(64)) reg9 (.D(multiplexer_30_out), .en(LE9), .clk(clock_10_out), .Q(OUT9));  // open: clr
  Clock clock_10 (.out(clock_10_out));
  Multiplexer #(.select(4), .width(64)) multiplexer_31 (
    .in0(OUT0), .in1(OUT1), .in2(OUT2), .in3(OUT3), .in4(OUT4), .in5(OUT5), .in6(OUT6), .in7(OUT7),
    .in8(OUT8), .in9(OUT9), .in10(OUT10), .in11(OUT11), .in12(OUT12), .in13(OUT13), .in14(OUT14),
    .in15(OUT15), .out(OUTA5), .sel(DA5));
  Multiplexer #(.select(4), .width(64)) multiplexer_32 (
    .in0(OUT0), .in1(OUT1), .in2(OUT2), .in3(OUT3), .in4(OUT4), .in5(OUT5), .in6(OUT6), .in7(OUT7),
    .in8(OUT8), .in9(OUT9), .in10(OUT10), .in11(OUT11), .in12(OUT12), .in13(OUT13), .in14(OUT14),
    .in15(OUT15), .out(OUTA13), .sel(DA13));
  Multiplexer #(.select(4), .width(64)) multiplexer_33 (
    .in0(IN0), .in1(IN1), .in2(IN2), .in3(IN3), .in4(IN4), .in5(IN5), .in6(IN6), .in7(IN7), .in8(IN8),
    .in9(IN9), .in10(IN10), .in11(IN11), .in12(IN12), .in13(IN13), .in14(IN14), .in15(IN15),
    .out(multiplexer_33_out), .sel(A10));
  Register #(.width(64)) reg10 (.D(multiplexer_33_out), .en(LE10), .clk(clock_11_out), .Q(OUT10));  // open: clr
  Clock clock_11 (.out(clock_11_out));
  Multiplexer #(.select(4), .width(64)) multiplexer_34 (
    .in0(OUT0), .in1(OUT1), .in2(OUT2), .in3(OUT3), .in4(OUT4), .in5(OUT5), .in6(OUT6), .in7(OUT7),
    .in8(OUT8), .in9(OUT9), .in10(OUT10), .in11(OUT11), .in12(OUT12), .in13(OUT13), .in14(OUT14),
    .in15(OUT15), .out(OUTB5), .sel(DB5));
  Multiplexer #(.select(4), .width(64)) multiplexer_35 (
    .in0(OUT0), .in1(OUT1), .in2(OUT2), .in3(OUT3), .in4(OUT4), .in5(OUT5), .in6(OUT6), .in7(OUT7),
    .in8(OUT8), .in9(OUT9), .in10(OUT10), .in11(OUT11), .in12(OUT12), .in13(OUT13), .in14(OUT14),
    .in15(OUT15), .out(OUTB13), .sel(DB13));
  Multiplexer #(.select(4), .width(64)) multiplexer_36 (
    .in0(IN0), .in1(IN1), .in2(IN2), .in3(IN3), .in4(IN4), .in5(IN5), .in6(IN6), .in7(IN7), .in8(IN8),
    .in9(IN9), .in10(IN10), .in11(IN11), .in12(IN12), .in13(IN13), .in14(IN14), .in15(IN15),
    .out(multiplexer_36_out), .sel(A11));
  Register #(.width(64)) reg11 (.D(multiplexer_36_out), .en(LE11), .clk(clock_12_out), .Q(OUT11));  // open: clr
  Clock clock_12 (.out(clock_12_out));
  Multiplexer #(.select(4), .width(64)) multiplexer_37 (
    .in0(OUT0), .in1(OUT1), .in2(OUT2), .in3(OUT3), .in4(OUT4), .in5(OUT5), .in6(OUT6), .in7(OUT7),
    .in8(OUT8), .in9(OUT9), .in10(OUT10), .in11(OUT11), .in12(OUT12), .in13(OUT13), .in14(OUT14),
    .in15(OUT15), .out(OUTA6), .sel(DA6));
  Multiplexer #(.select(4), .width(64)) multiplexer_38 (
    .in0(OUT0), .in1(OUT1), .in2(OUT2), .in3(OUT3), .in4(OUT4), .in5(OUT5), .in6(OUT6), .in7(OUT7),
    .in8(OUT8), .in9(OUT9), .in10(OUT10), .in11(OUT11), .in12(OUT12), .in13(OUT13), .in14(OUT14),
    .in15(OUT15), .out(OUTA14), .sel(DA14));
  Multiplexer #(.select(4), .width(64)) multiplexer_39 (
    .in0(IN0), .in1(IN1), .in2(IN2), .in3(IN3), .in4(IN4), .in5(IN5), .in6(IN6), .in7(IN7), .in8(IN8),
    .in9(IN9), .in10(IN10), .in11(IN11), .in12(IN12), .in13(IN13), .in14(IN14), .in15(IN15),
    .out(multiplexer_39_out), .sel(A12));
  Register #(.width(64)) reg12 (.D(multiplexer_39_out), .en(LE12), .clk(clock_13_out), .Q(OUT12));  // open: clr
  Clock clock_13 (.out(clock_13_out));
  Multiplexer #(.select(4), .width(64)) multiplexer_40 (
    .in0(OUT0), .in1(OUT1), .in2(OUT2), .in3(OUT3), .in4(OUT4), .in5(OUT5), .in6(OUT6), .in7(OUT7),
    .in8(OUT8), .in9(OUT9), .in10(OUT10), .in11(OUT11), .in12(OUT12), .in13(OUT13), .in14(OUT14),
    .in15(OUT15), .out(OUTB6), .sel(DB6));
  Multiplexer #(.select(4), .width(64)) multiplexer_41 (
    .in0(OUT0), .in1(OUT1), .in2(OUT2), .in3(OUT3), .in4(OUT4), .in5(OUT5), .in6(OUT6), .in7(OUT7),
    .in8(OUT8), .in9(OUT9), .in10(OUT10), .in11(OUT11), .in12(OUT12), .in13(OUT13), .in14(OUT14),
    .in15(OUT15), .out(OUTB14), .sel(DB14));
  Multiplexer #(.select(4), .width(64)) multiplexer_42 (
    .in0(IN0), .in1(IN1), .in2(IN2), .in3(IN3), .in4(IN4), .in5(IN5), .in6(IN6), .in7(IN7), .in8(IN8),
    .in9(IN9), .in10(IN10), .in11(IN11), .in12(IN12), .in13(IN13), .in14(IN14), .in15(IN15),
    .out(multiplexer_42_out), .sel(A13));
  Register #(.width(64)) reg13 (.D(multiplexer_42_out), .en(LE13), .clk(clock_14_out), .Q(OUT13));  // open: clr
  Clock clock_14 (.out(clock_14_out));
  Multiplexer #(.select(4), .width(64)) multiplexer_43 (
    .in0(OUT0), .in1(OUT1), .in2(OUT2), .in3(OUT3), .in4(OUT4), .in5(OUT5), .in6(OUT6), .in7(OUT7),
    .in8(OUT8), .in9(OUT9), .in10(OUT10), .in11(OUT11), .in12(OUT12), .in13(OUT13), .in14(OUT14),
    .in15(OUT15), .out(OUTA7), .sel(DA7));
  Multiplexer #(.select(4), .width(64)) multiplexer_44 (
    .in0(OUT0), .in1(OUT1), .in2(OUT2), .in3(OUT3), .in4(OUT4), .in5(OUT5), .in6(OUT6), .in7(OUT7),
    .in8(OUT8), .in9(OUT9), .in10(OUT10), .in11(OUT11), .in12(OUT12), .in13(OUT13), .in14(OUT14),
    .in15(OUT15), .out(OUTA15), .sel(DA15));
  Multiplexer #(.select(4), .width(64)) multiplexer_45 (
    .in0(IN0), .in1(IN1), .in2(IN2), .in3(IN3), .in4(IN4), .in5(IN5), .in6(IN6), .in7(IN7), .in8(IN8),
    .in9(IN9), .in10(IN10), .in11(IN11), .in12(IN12), .in13(IN13), .in14(IN14), .in15(IN15),
    .out(multiplexer_45_out), .sel(A14));
  Register #(.width(64)) reg14 (.D(multiplexer_45_out), .en(LE14), .clk(clock_15_out), .Q(OUT14));  // open: clr
  Clock clock_15 (.out(clock_15_out));
  Multiplexer #(.select(4), .width(64)) multiplexer_46 (
    .in0(OUT0), .in1(OUT1), .in2(OUT2), .in3(OUT3), .in4(OUT4), .in5(OUT5), .in6(OUT6), .in7(OUT7),
    .in8(OUT8), .in9(OUT9), .in10(OUT10), .in11(OUT11), .in12(OUT12), .in13(OUT13), .in14(OUT14),
    .in15(OUT15), .out(OUTB7), .sel(DB7));
  Multiplexer #(.select(4), .width(64)) multiplexer_47 (
    .in0(OUT0), .in1(OUT1), .in2(OUT2), .in3(OUT3), .in4(OUT4), .in5(OUT5), .in6(OUT6), .in7(OUT7),
    .in8(OUT8), .in9(OUT9), .in10(OUT10), .in11(OUT11), .in12(OUT12), .in13(OUT13), .in14(OUT14),
    .in15(OUT15), .out(OUTB15), .sel(DB15));
  Multiplexer #(.select(4), .width(64)) multiplexer_48 (
    .in0(IN0), .in1(IN1), .in2(IN2), .in3(IN3), .in4(IN4), .in5(IN5), .in6(IN6), .in7(IN7), .in8(IN8),
    .in9(IN9), .in10(IN10), .in11(IN11), .in12(IN12), .in13(IN13), .in14(IN14), .in15(IN15),
    .out(multiplexer_48_out), .sel(A15));
  Register #(.width(64)) reg15 (.D(multiplexer_48_out), .en(LE15), .clk(clock_16_out), .Q(OUT15));  // open: clr
  Clock clock_16 (.out(clock_16_out));
endmodule
