// Logisim project muxrisccore.circ as structural Verilog: 2 circuits, main circuit core
module core (
);

  wire alu_1_we, and_1_out, and_2_out, and_3_out, and_4_out, and_5_out, and_6_out, and_7_out, and_8_out,
       cart1_p29, clock_1_out, clock_5_out, clock_6_out, clock_8_out, clock_9_out, comparator_1_eq,
       comparator_2_gt, comparator_3_eq, comparator_4_eq, comparator_5_eq, comparator_6_eq, comparator_7_eq,
       comparator_8_eq, comparator_9_eq, comparator_10_eq, comparator_11_eq, comparator_12_eq,
       comparator_13_eq, comparator_14_eq, comparator_15_eq, comparator_16_eq, comparator_17_eq,
       comparator_18_eq, comparator_18_gt, comparator_18_lt, comparator_19_eq, comparator_19_gt,
       comparator_19_lt, comparator_20_eq, not_1_out, not_2_out, not_3_out, not_4_out, not_5_out, not_6_out,
       not_7_out, or_1_out, or_2_out, or_4_out, register_1_q, regX_p2, regX_p11, rgb_video_1_p1;
  wire [1:0] bitselector_22_out, bitselector_27_out;
  wire [3:0] bitselector_7_out, bitselector_8_out, bitselector_12_out, bitselector_13_out;
  wire [7:0] bitselector_5_out, bitselector_6_out, bitselector_11_out, bitselector_14_out,
       bitselector_17_out, bitselector_19_out, bitselector_21_out;
  wire [8:0] bitselector_23_out, bitselector_25_out;
  wire [15:0] bitselector_1_out, bitselector_2_out, bitselector_3_out, bitselector_4_out, bitselector_10_out,
       bitselector_15_out, bitselector_16_out, bitselector_18_out;
  wire [17:0] bitselector_24_out;
  wire [23:0] bitselector_26_out, bitselector_29_out, ram1_p2;
  wire [31:0] bitselector_9_out, counter_1_q;
  wire [63:0] alu_1_outx, alu_2_outx, alu_3_outx, alu_4_outx, alu_5_outx, alu_6_outx, alu_7_outx, alu_8_outx,
       cart1_p31, cart1_p32, cart1_p33, cart1_p34, cart1_p35, cart1_p36, cart1_p37, cart1_p38, cart1_p39,
       counter_2_q, multiplexer_2_out, multiplexer_4_out, multiplexer_5_out, multiplexer_8_out,
       multiplexer_10_out, multiplexer_12_out, multiplexer_14_out, multiplexer_16_out, multiplexer_17_out,
       multiplexer_18_out, multiplexer_19_out, multiplexer_20_out, multiplexer_21_out, multiplexer_22_out,
       multiplexer_23_out, multiplexer_24_out, multiplexer_25_out, multiplexer_26_out, ram1_p3, regX_p12,
       regX_p13, regX_p14, regX_p15, regX_p16, regX_p17, regX_p18, regX_p19, regX_p20, regX_p21, regX_p22,
       regX_p23, regX_p24, regX_p25, regX_p26, regX_p27, regY_p10, regY_p11, regY_p12, regY_p13, regY_p14,
       regY_p15, regY_p16, regY_p17, regZ_p10, regZ_p11, regZ_p12, regZ_p13, regZ_p14, regZ_p15, regZ_p16,
       regZ_p17, rom1_p9, rom1_p10, rom1_p11, rom1_p12, rom1_p13, rom1_p14, rom1_p15, rom1_p16;

  BitSelector #(.group(16), .width(64)) bitselector_1 (.in(multiplexer_18_out), .out(bitselector_1_out), .sel(2'b11));
  BitSelector #(.group(16), .width(64)) bitselector_2 (.in(multiplexer_18_out), .out(bitselector_2_out), .sel(2'b10));
  BitSelector #(.group(16), .width(64)) bitselector_3 (.in(multiplexer_18_out), .out(bitselector_3_out), .sel(2'b01));
  BitSelector #(.group(16), .width(64)) bitselector_4 (.in(multiplexer_18_out), .out(bitselector_4_out), .sel(2'b00));
  BitSelector #(.group(8), .width(16)) bitselector_5 (.in(bitselector_4_out), .out(bitselector_5_out), .sel(1'b1));
  BitSelector #(.group(8), .width(16)) bitselector_6 (.in(bitselector_4_out), .out(bitselector_6_out), .sel(1'b0));
  BitSelector #(.group(4)) bitselector_7 (.in(bitselector_6_out), .out(bitselector_7_out), .sel(1'b0));
  BitSelector #(.group(4)) bitselector_8 (.in(bitselector_6_out), .out(bitselector_8_out), .sel(1'b1));
  BitSelector #(.group(32), .width(64)) bitselector_9 (.in(regY_p10), .out(bitselector_9_out), .sel(1'b0));
  BitSelector #(.group(16), .width(64)) bitselector_10 (.in(regY_p10), .out(bitselector_10_out), .sel(2'b00));
  BitSelector #(.group(8), .width(64)) bitselector_11 (.in(regY_p10), .out(bitselector_11_out), .sel(3'b000));
  Comparator #(.mode("unsigned")) comparator_1 (
    .a(bitselector_6_out), .b(8'ha0), .eq(comparator_1_eq));  // open: gt, lt
  BitSelector #(.group(4)) bitselector_12 (.in(bitselector_6_out), .out(bitselector_12_out), .sel(1'b0));
  BitSelector #(.group(4)) bitselector_13 (.in(bitselector_6_out), .out(bitselector_13_out), .sel(1'b1));
  Comparator #(.mode("unsigned"), .width(4)) comparator_2 (
    .a(bitselector_7_out), .b(4'b0000), .gt(comparator_2_gt));  // open: eq, lt
  Comparator #(.mode("unsigned")) comparator_3 (
    .a(bitselector_6_out), .b({8{1'b0}}), .eq(comparator_3_eq));  // open: gt, lt
  Counter #(.max('hffffffff), .width(32)) counter_1 (
    .load(or_1_out), .D({32{1'b0}}), .count(comparator_3_eq), .Q(counter_1_q), .clk(clock_1_out));  // open: carry, up, clr
  Clock clock_1 (.out(clock_1_out));
  Comparator #(.mode("unsigned")) comparator_4 (
    .a(bitselector_6_out), .b(8'h10), .eq(comparator_4_eq));  // open: gt, lt
  Comparator #(.mode("unsigned")) comparator_5 (
    .a(bitselector_6_out), .b(8'h20), .eq(comparator_5_eq));  // open: gt, lt
  Comparator #(.mode("unsigned"), .width(64)) comparator_6 (
    .a(regY_p10), .b({64{1'b0}}), .eq(comparator_6_eq));  // open: gt, lt
  Comparator #(.mode("unsigned")) comparator_7 (
    .a(bitselector_6_out), .b(8'h30), .eq(comparator_7_eq));  // open: gt, lt
  Comparator #(.mode("unsigned"), .width(32)) comparator_8 (
    .a(bitselector_9_out), .b({32{1'b0}}), .eq(comparator_8_eq));  // open: gt, lt
  Comparator #(.mode("unsigned")) comparator_9 (
    .a(bitselector_6_out), .b(8'h40), .eq(comparator_9_eq));  // open: gt, lt
  Comparator #(.mode("unsigned"), .width(16)) comparator_10 (
    .a(bitselector_10_out), .b({16{1'b0}}), .eq(comparator_10_eq));  // open: gt, lt
  Comparator #(.mode("unsigned")) comparator_11 (
    .a(bitselector_6_out), .b(8'h50), .eq(comparator_11_eq));  // open: gt, lt
  Comparator #(.mode("unsigned")) comparator_12 (
    .a(bitselector_11_out), .b({8{1'b0}}), .eq(comparator_12_eq));  // open: gt, lt
  Comparator #(.mode("unsigned")) comparator_13 (
    .a(bitselector_6_out), .b(8'h60), .eq(comparator_13_eq));  // open: gt, lt
  Comparator #(.mode("unsigned")) comparator_14 (
    .a(bitselector_6_out), .b(8'h70), .eq(comparator_14_eq));  // open: gt, lt
  Comparator #(.mode("unsigned")) comparator_15 (
    .a(bitselector_6_out), .b(8'h80), .eq(comparator_15_eq));  // open: gt, lt
  Comparator #(.mode("unsigned")) comparator_16 (
    .a(bitselector_6_out), .b(8'h90), .eq(comparator_16_eq));  // open: gt, lt
  Comparator #(.mode("unsigned")) comparator_17 (
    .a(bitselector_6_out), .b(8'hb0), .eq(comparator_17_eq));  // open: gt, lt
  Comparator #(.mode("unsigned"), .width(32)) comparator_18 (
    .a(counter_1_q), .b({bitselector_2_out, bitselector_3_out}), .gt(comparator_18_gt),
    .eq(comparator_18_eq), .lt(comparator_18_lt));
  and and_1 (and_1_out, comparator_5_eq, not_1_out);
  not not_1 (not_1_out, comparator_6_eq);
  and and_2 (and_2_out, comparator_7_eq, not_2_out);
  not not_2 (not_2_out, comparator_8_eq);
  and and_3 (and_3_out, comparator_9_eq, not_3_out);
  not not_3 (not_3_out, comparator_10_eq);
  and and_4 (and_4_out, comparator_11_eq, not_4_out);
  not not_4 (not_4_out, comparator_12_eq);
  BitSelector #(.group(8), .width(16)) bitselector_14 (.in(bitselector_3_out), .out(bitselector_14_out), .sel(1'b0));
  // RAM #(.addrWidth(16), .dataWidth(64), .enables("line"), .line("octo"), .misaligned("true")) regX: pin names not known; wires that end beside it: bitselector_1_out, regX_p2, regX_p2, bitselector_5_out[1], bitselector_5_out[2], bitselector_5_out[3], bitselector_5_out[4], bitselector_5_out[5], bitselector_5_out[6], bitselector_5_out[7], regX_p11, regX_p12, regX_p13, regX_p14, regX_p15, regX_p16, regX_p17, regX_p18, regX_p19, regX_p20, regX_p21, regX_p22, regX_p23, regX_p24, regX_p25, regX_p26, regX_p27
  Clock clock_2 (.out(regX_p11));
  or or_1 (or_1_out, comparator_18_gt, comparator_18_eq);
  and and_5 (and_5_out, comparator_18_lt, comparator_3_eq);
  or or_2 (or_2_out, comparator_4_eq, and_1_out, and_2_out, and_3_out, and_4_out);
  or or_3 (regX_p2, comparator_13_eq, comparator_14_eq, comparator_15_eq, comparator_16_eq, comparator_1_eq, alu_1_we);
  Multiplexer #(.width(64)) multiplexer_1 (
    .in0(multiplexer_2_out), .in1(alu_1_outx), .out(regX_p12), .sel(comparator_2_gt));
  Multiplexer #(.select(4), .width(64)) multiplexer_2 (
    .in6({{32{1'b0}}, bitselector_2_out, bitselector_3_out}),
    .in7({bitselector_2_out, bitselector_3_out, bitselector_2_out, bitselector_3_out}),
    .in8({bitselector_3_out, bitselector_3_out, bitselector_3_out, bitselector_3_out}),
    .in9({bitselector_14_out, bitselector_14_out, bitselector_14_out, bitselector_14_out, bitselector_14_out, bitselector_14_out, bitselector_14_out, bitselector_14_out}),
    .in10(multiplexer_19_out), .out(multiplexer_2_out), .sel(bitselector_8_out));  // open: in0, in1, in2, in3, in4, in5, in11, in12, in13, in14, in15
  alu alu_1 (
    .argX(regX_p20), .argY(regY_p10), .argZ(regZ_p10), .op(bitselector_12_out), .\var (bitselector_13_out),
    .outX(alu_1_outx), .we(alu_1_we));
  alu alu_2 (
    .argX(regX_p21), .argY(regY_p11), .argZ(regZ_p11), .op(bitselector_12_out), .\var (bitselector_13_out),
    .outX(alu_2_outx));  // open: we
  // DualRAM #(.addrWidth(16), .dataWidth(64), .enables("line"), .line("octo"), .misaligned("true"), .\type ("nonvolatile")) regY: pin names not known; wires that end beside it: bitselector_2_out, bitselector_1_out, regX_p2, regX_p2, bitselector_5_out[1], bitselector_5_out[2], bitselector_5_out[3], bitselector_5_out[4], bitselector_5_out[5], regY_p10, regY_p11, regY_p12, regY_p13, regY_p14, regY_p15, regY_p16, regY_p17
  Clock clock_3 ();  // open: out
  Multiplexer #(.width(64)) multiplexer_3 (
    .in0(multiplexer_4_out), .in1(alu_2_outx), .out(regX_p13), .sel(comparator_2_gt));
  Multiplexer #(.select(4), .width(64)) multiplexer_4 (
    .in6({{32{1'b0}}, bitselector_2_out, bitselector_3_out}),
    .in7({bitselector_2_out, bitselector_3_out, bitselector_2_out, bitselector_3_out}),
    .in8({bitselector_3_out, bitselector_3_out, bitselector_3_out, bitselector_3_out}),
    .in9({bitselector_14_out, bitselector_14_out, bitselector_14_out, bitselector_14_out, bitselector_14_out, bitselector_14_out, bitselector_14_out, bitselector_14_out}),
    .in10(multiplexer_20_out), .out(multiplexer_4_out), .sel(bitselector_8_out));  // open: in0, in1, in2, in3, in4, in5, in11, in12, in13, in14, in15
  Multiplexer #(.select(4), .width(64)) multiplexer_5 (
    .in6({{32{1'b0}}, bitselector_2_out, bitselector_3_out}),
    .in7({bitselector_2_out, bitselector_3_out, bitselector_2_out, bitselector_3_out}),
    .in8({bitselector_3_out, bitselector_3_out, bitselector_3_out, bitselector_3_out}),
    .in9({bitselector_14_out, bitselector_14_out, bitselector_14_out, bitselector_14_out, bitselector_14_out, bitselector_14_out, bitselector_14_out, bitselector_14_out}),
    .in10(multiplexer_21_out), .out(multiplexer_5_out), .sel(bitselector_8_out));  // open: in0, in1, in2, in3, in4, in5, in11, in12, in13, in14, in15
  alu alu_3 (
    .argX(regX_p22), .argY(regY_p12), .argZ(regZ_p12), .op(bitselector_12_out), .\var (bitselector_13_out),
    .outX(alu_3_outx));  // open: we
  Multiplexer #(.width(64)) multiplexer_6 (
    .in0(multiplexer_5_out), .in1(alu_3_outx), .out(regX_p14), .sel(comparator_2_gt));
  alu alu_4 (
    .argX(regX_p23), .argY(regY_p13), .argZ(regZ_p13), .op(bitselector_12_out), .\var (bitselector_13_out),
    .outX(alu_4_outx));  // open: we
  Multiplexer #(.width(64)) multiplexer_7 (
    .in0(multiplexer_8_out), .in1(alu_4_outx), .out(regX_p15), .sel(comparator_2_gt));
  Multiplexer #(.select(4), .width(64)) multiplexer_8 (
    .in6({{32{1'b0}}, bitselector_2_out, bitselector_3_out}),
    .in7({bitselector_2_out, bitselector_3_out, bitselector_2_out, bitselector_3_out}),
    .in8({bitselector_3_out, bitselector_3_out, bitselector_3_out, bitselector_3_out}),
    .in9({bitselector_14_out, bitselector_14_out, bitselector_14_out, bitselector_14_out, bitselector_14_out, bitselector_14_out, bitselector_14_out, bitselector_14_out}),
    .in10(multiplexer_22_out), .out(multiplexer_8_out), .sel(bitselector_8_out));  // open: in0, in1, in2, in3, in4, in5, in11, in12, in13, in14, in15
  alu alu_5 (
    .argX(regX_p24), .argY(regY_p14), .argZ(regZ_p14), .op(bitselector_12_out), .\var (bitselector_13_out),
    .outX(alu_5_outx));  // open: we
  // DualRAM #(.addrWidth(16), .dataWidth(64), .enables("line"), .line("octo"), .misaligned("true"), .\type ("nonvolatile")) regZ: pin names not known; wires that end beside it: bitselector_3_out, bitselector_1_out, regX_p2, regX_p2, bitselector_5_out[1], bitselector_5_out[2], bitselector_5_out[3], bitselector_5_out[4], bitselector_5_out[5], regZ_p10, regZ_p11, regZ_p12, regZ_p13, regZ_p14, regZ_p15, regZ_p16, regZ_p17
  Clock clock_4 ();  // open: out
  Multiplexer #(.width(64)) multiplexer_9 (
    .in0(multiplexer_10_out), .in1(alu_5_outx), .out(regX_p16), .sel(comparator_2_gt));
  Multiplexer #(.select(4), .width(64)) multiplexer_10 (
    .in6({{32{1'b0}}, bitselector_2_out, bitselector_3_out}),
    .in7({bitselector_2_out, bitselector_3_out, bitselector_2_out, bitselector_3_out}),
    .in8({bitselector_3_out, bitselector_3_out, bitselector_3_out, bitselector_3_out}),
    .in9({bitselector_14_out, bitselector_14_out, bitselector_14_out, bitselector_14_out, bitselector_14_out, bitselector_14_out, bitselector_14_out, bitselector_14_out}),
    .in10(multiplexer_23_out), .out(multiplexer_10_out), .sel(bitselector_8_out));  // open: in0, in1, in2, in3, in4, in5, in11, in12, in13, in14, in15
  Multiplexer #(.width(64)) multiplexer_11 (
    .in0(multiplexer_12_out), .in1(alu_6_outx), .out(regX_p17), .sel(comparator_2_gt));
  Multiplexer #(.select(4), .width(64)) multiplexer_12 (
    .in6({{32{1'b0}}, bitselector_2_out, bitselector_3_out}),
    .in7({bitselector_2_out, bitselector_3_out, bitselector_2_out, bitselector_3_out}),
    .in8({bitselector_3_out, bitselector_3_out, bitselector_3_out, bitselector_3_out}),
    .in9({bitselector_14_out, bitselector_14_out, bitselector_14_out, bitselector_14_out, bitselector_14_out, bitselector_14_out, bitselector_14_out, bitselector_14_out}),
    .in10(multiplexer_24_out), .out(multiplexer_12_out), .sel(bitselector_8_out));  // open: in0, in1, in2, in3, in4, in5, in11, in12, in13, in14, in15
  alu alu_6 (
    .argX(regX_p25), .argY(regY_p15), .argZ(regZ_p15), .op(bitselector_12_out), .\var (bitselector_13_out),
    .outX(alu_6_outx));  // open: we
  alu alu_7 (
    .argX(regX_p26), .argY(regY_p16), .argZ(regZ_p16), .op(bitselector_12_out), .\var (bitselector_13_out),
    .outX(alu_7_outx));  // open: we
  Multiplexer #(.width(64)) multiplexer_13 (
    .in0(multiplexer_14_out), .in1(alu_7_outx), .out(regX_p18), .sel(comparator_2_gt));
  Multiplexer #(.select(4), .width(64)) multiplexer_14 (
    .in6({{32{1'b0}}, bitselector_2_out, bitselector_3_out}),
    .in7({bitselector_2_out, bitselector_3_out, bitselector_2_out, bitselector_3_out}),
    .in8({bitselector_3_out, bitselector_3_out, bitselector_3_out, bitselector_3_out}),
    .in9({bitselector_14_out, bitselector_14_out, bitselector_14_out, bitselector_14_out, bitselector_14_out, bitselector_14_out, bitselector_14_out, bitselector_14_out}),
    .in10(multiplexer_25_out), .out(multiplexer_14_out), .sel(bitselector_8_out));  // open: in0, in1, in2, in3, in4, in5, in11, in12, in13, in14, in15
  alu alu_8 (
    .argX(regX_p27), .argY(regY_p17), .argZ(regZ_p17), .op(bitselector_12_out), .\var (bitselector_13_out),
    .outX(alu_8_outx));  // open: we
  Multiplexer #(.width(64)) multiplexer_15 (
    .in0(multiplexer_16_out), .in1(alu_8_outx), .out(regX_p19), .sel(comparator_2_gt));
  Multiplexer #(.select(4), .width(64)) multiplexer_16 (
    .in6({{32{1'b0}}, bitselector_2_out, bitselector_3_out}),
    .in7({bitselector_2_out, bitselector_3_out, bitselector_2_out, bitselector_3_out}),
    .in8({bitselector_3_out, bitselector_3_out, bitselector_3_out, bitselector_3_out}),
    .in9({bitselector_14_out, bitselector_14_out, bitselector_14_out, bitselector_14_out, bitselector_14_out, bitselector_14_out, bitselector_14_out, bitselector_14_out}),
    .in10(multiplexer_26_out), .out(multiplexer_16_out), .sel(bitselector_8_out));  // open: in0, in1, in2, in3, in4, in5, in11, in12, in13, in14, in15
  BitSelector #(.group(16), .width(64)) bitselector_15 (.in(regX_p20), .out(bitselector_15_out), .sel(2'b00));
  BitSelector #(.group(16), .width(64)) bitselector_16 (.in(regX_p20), .out(bitselector_16_out), .sel(2'b01));
  BitSelector #(.group(8), .width(16)) bitselector_17 (.in(bitselector_15_out), .out(bitselector_17_out), .sel(1'b0));
  BitSelector #(.group(16), .width(64)) bitselector_18 (.in(regX_p20), .out(bitselector_18_out), .sel(2'b10));
  BitSelector #(.group(8), .width(16)) bitselector_19 (.in(bitselector_16_out), .out(bitselector_19_out), .sel(1'b0));
  BitSelector #(.group(16), .width(64)) bitselector_20 (.in(regX_p20), .sel(2'b11));  // open: out
  BitSelector #(.group(8), .width(16)) bitselector_21 (.in(bitselector_18_out), .out(bitselector_21_out), .sel(1'b0));
  Register #(.trigger("falling"), .width(1)) register_1 (
    .D(1'b1), .en(not_5_out), .Q(register_1_q), .clk(clock_5_out));  // open: clr
  Clock clock_5 (.out(clock_5_out));
  BitSelector #(.group(2), .width(64)) bitselector_22 (.in(regY_p10), .out(bitselector_22_out), .sel({5{1'b1}}));
  BitSelector #(.group(9), .width(64)) bitselector_23 (.in(regY_p10), .out(bitselector_23_out), .sel(3'b001));
  BitSelector #(.group(18), .width(64)) bitselector_24 (.in(regY_p10), .out(bitselector_24_out), .sel(2'b00));
  Multiplexer #(.width(64)) multiplexer_17 (
    .in0(64'hc000000000000000), .in1(regX_p20), .out(multiplexer_17_out), .sel(register_1_q));
  or or_4 (or_4_out, or_2_out, not_5_out);
  not not_5 (not_5_out, register_1_q);
  and and_6 (and_6_out, comparator_17_eq, comparator_19_gt);
  Comparator #(.mode("unsigned"), .width(2)) comparator_19 (
    .a(bitselector_22_out), .b(2'b01), .gt(comparator_19_gt), .eq(comparator_19_eq), .lt(comparator_19_lt));
  BitSelector #(.group(9), .width(64)) bitselector_25 (.in(regY_p10), .out(bitselector_25_out), .sel(3'b000));
  not not_6 (not_6_out, and_5_out);
  Clock clock_6 (.out(clock_6_out));
  not not_7 (not_7_out, comparator_19_lt);
  // RGB_Video #(.cursor("No Cursor"), .height(512), .scale(1), .width(512)) rgb_video_1: pin names not known; wires that end beside it: rgb_video_1_p1, and_6_out, bitselector_23_out, bitselector_25_out, {bitselector_17_out, bitselector_19_out, bitselector_21_out}
  Clock clock_7 (.out(rgb_video_1_p1));
  BitSelector #(.group(24), .width(64)) bitselector_26 (.in(counter_2_q), .out(bitselector_26_out), .sel(2'b00));
  Counter #(.max('hffffffffffffffff), .trigger("falling"), .width(64)) counter_2 (
    .load(or_4_out), .D(multiplexer_17_out), .count(not_6_out), .Q(counter_2_q), .clk(clock_6_out));  // open: carry, up, clr
  and and_7 (and_7_out, comparator_19_lt, comparator_17_eq);
  and and_8 (and_8_out, comparator_19_eq, comparator_17_eq);
  RAM #(.addrWidth(18), .dataWidth(64), .enables("line")) disp1 (
    .addr(bitselector_24_out), .we(and_6_out), .clk(clock_8_out), .din(regX_p20));  // open: dout
  Clock clock_8 (.out(clock_8_out));
  BitSelector #(.group(2), .width(64)) bitselector_27 (.in(counter_2_q), .out(bitselector_27_out), .sel({5{1'b1}}));
  // DualRAM #(.addrWidth(24), .dataWidth(64), .enables("line"), .line("octo"), .misaligned("true"), .\type ("nonvolatile")) ram1: pin names not known; wires that end beside it: bitselector_26_out, ram1_p2, ram1_p3
  BitSelector #(.group(24), .width(64)) bitselector_28 (.in(regY_p10), .out(ram1_p2), .sel(2'b00));
  Clock clock_9 (.out(clock_9_out));
  BitSelector #(.group(24), .width(64)) bitselector_29 (.in(regY_p10), .out(bitselector_29_out), .sel(2'b00));
  // RAM #(.addrWidth(24), .dataWidth(64), .enables("line"), .line("octo"), .misaligned("true")) cart1: pin names not known; wires that end beside it: and_7_out, and_7_out, bitselector_5_out[1], bitselector_5_out[2], bitselector_5_out[3], bitselector_5_out[4], bitselector_5_out[5], bitselector_5_out[6], bitselector_5_out[7], clock_9_out, regX_p20, regX_p21, regX_p22, regX_p23, regX_p24, regX_p25, regX_p26, regX_p27, bitselector_29_out, and_8_out, and_8_out, bitselector_5_out[1], bitselector_5_out[2], bitselector_5_out[3], bitselector_5_out[4], bitselector_5_out[5], bitselector_5_out[6], bitselector_5_out[7], cart1_p29, regX_p20, cart1_p31, cart1_p32, cart1_p33, cart1_p34, cart1_p35, cart1_p36, cart1_p37, cart1_p38, cart1_p39
  Clock clock_10 (.out(cart1_p29));
  // ROM #(.addrWidth(24), .dataWidth(64), .line("octo"), .misaligned("true")) rom1: pin names not known; wires that end beside it: regX_p21, regX_p22, regX_p23, regX_p24, regX_p25, regX_p26, regX_p27, bitselector_26_out, rom1_p9, rom1_p10, rom1_p11, rom1_p12, rom1_p13, rom1_p14, rom1_p15, rom1_p16
  Comparator #(.mode("unsigned"), .width(2)) comparator_20 (
    .a(bitselector_27_out), .b(2'b11), .eq(comparator_20_eq));  // open: gt, lt
  Multiplexer #(.width(64)) multiplexer_18 (
    .in0(ram1_p3), .in1(rom1_p16), .out(multiplexer_18_out), .sel(comparator_20_eq));
  Multiplexer #(.width(64)) multiplexer_19 (
    .in0(cart1_p31), .in1(cart1_p39), .out(multiplexer_19_out), .sel(not_7_out));
  Multiplexer #(.width(64)) multiplexer_20 (.in0(cart1_p32), .in1(rom1_p9), .out(multiplexer_20_out), .sel(not_7_out));
  Multiplexer #(.width(64)) multiplexer_21 (.in0(cart1_p33), .in1(rom1_p10), .out(multiplexer_21_out), .sel(not_7_out));
  Multiplexer #(.width(64)) multiplexer_22 (.in0(cart1_p34), .in1(rom1_p11), .out(multiplexer_22_out), .sel(not_7_out));
  Multiplexer #(.width(64)) multiplexer_23 (.in0(cart1_p35), .in1(rom1_p12), .out(multiplexer_23_out), .sel(not_7_out));
  Multiplexer #(.width(64)) multiplexer_24 (.in0(cart1_p36), .in1(rom1_p13), .out(multiplexer_24_out), .sel(not_7_out));
  Multiplexer #(.width(64)) multiplexer_25 (.in0(cart1_p37), .in1(rom1_p14), .out(multiplexer_25_out), .sel(not_7_out));
  Multiplexer #(.width(64)) multiplexer_26 (.in0(cart1_p38), .in1(rom1_p15), .out(multiplexer_26_out), .sel(not_7_out));

  // Notes on the sheet:
  //   contents of rom1 (hex, n*v repeats v):
  //   400000000060 2000000200060 3000000080360 5000000100060 6c00000000060 a0000000f0060 b000000000060
  //   6000600020002 60006000a0072 20002 70000000000a0 7000700050012 c000700000001 b000c00000020
  //   1000000030004 1000100030004 4000400030004 1000010000ffa0 1000040000ffb0 8000400070024 9000800000011
  //   6000900000020 b000000000010
endmodule

module alu (
  input  [63:0] argX,
  input  [63:0] argY,
  input  [63:0] argZ,
  input  [3:0] op,
  input  [3:0] \var ,
  output [63:0] outX,
  output we
);

  wire adder_1_cout, and_1_out, and_2_out, and_4_out, and_5_out, and_6_out, and_7_out, bitfinder_1_found,
       bitfinder_2_found, bitfinder_3_found, bitfinder_4_found, clock_1_out, clock_3_out, clock_4_out,
       comparator_1_eq, comparator_2_eq, comparator_2_lt, comparator_3_eq, comparator_4_eq, comparator_5_eq,
       comparator_6_eq, comparator_7_eq, comparator_8_eq, comparator_9_eq, comparator_10_eq,
       comparator_11_eq, comparator_11_lt, comparator_12_eq, comparator_13_eq, comparator_14_eq,
       comparator_15_eq, comparator_16_eq, comparator_17_eq, comparator_18_eq, comparator_19_eq,
       comparator_20_eq, comparator_21_eq, comparator_22_eq, comparator_22_lt, comparator_23_eq,
       comparator_23_lt, comparator_24_eq, comparator_25_eq, comparator_26_eq, comparator_26_lt,
       comparator_27_eq, comparator_27_lt, comparator_28_eq, comparator_28_lt, comparator_29_eq,
       comparator_29_lt, comparator_30_eq, comparator_31_eq, comparator_32_eq, comparator_33_eq,
       comparator_34_eq, comparator_34_lt, comparator_35_eq, comparator_35_lt, comparator_36_eq,
       comparator_36_lt, comparator_37_eq, comparator_37_lt, comparator_38_eq, comparator_38_lt,
       comparator_39_eq, comparator_39_lt, comparator_40_eq, comparator_40_lt, comparator_41_eq,
       comparator_41_lt, comparator_42_eq, comparator_43_eq, comparator_44_eq, comparator_45_eq,
       comparator_46_eq, comparator_47_eq, comparator_48_eq, comparator_49_eq, fpclassificator_1_p1,
       fpclassificator_1_p2, fpcomparator_1_p6, fpcomparator_1_p7, fpcomparator_2_p3, fpcomparator_2_p4,
       fpcomparator_3_p3, fpcomparator_3_p4, fpcomparator_4_p3, fpcomparator_4_p4, fpcomparator_5_p3,
       fpcomparator_5_p4, fpcomparator_6_p3, fpcomparator_6_p4, fpcomparator_7_p3, fpcomparator_7_p4,
       fpcomparator_8_p3, fpcomparator_8_p4, fpcomparator_9_p3, fpcomparator_9_p4, fpcomparator_10_p3,
       fpcomparator_10_p4, fpcomparator_11_p3, fpcomparator_11_p4, fpcomparator_12_p3, fpcomparator_12_p4,
       fpcomparator_13_p3, fpcomparator_13_p4, fpcomparator_14_p3, fpcomparator_14_p4, fpcomparator_15_p3,
       fpcomparator_15_p4, fpcomparator_16_p3, fpcomparator_16_p4, not_1_out, not_3_out, not_4_out,
       not_5_out, not_6_out, not_7_out, not_8_out, not_9_out, not_10_out, not_11_out, not_12_out, not_13_out,
       not_14_out, not_15_out, not_16_out, not_17_out, not_18_out, not_19_out, random_1_p1, subtractor_1_bout;
  wire [2:0] bitselector_2_out, bitselector_9_out, bitselector_10_out, bitselector_11_out,
       bitselector_12_out, bitselector_13_out, bitselector_14_out, bitselector_15_out, bitselector_16_out;
  wire [3:0] bitselector_5_out, bitselector_6_out, bitselector_7_out, bitselector_8_out;
  wire [4:0] bitselector_3_out, bitselector_4_out;
  wire [5:0] bitfinder_1_index, bitfinder_2_index, bitfinder_3_index, bitfinder_4_index, bitselector_1_out;
  wire [6:0] bitadder_1_out;
  wire [7:0] buffer_9_out, buffer_10_out, buffer_11_out, buffer_12_out, buffer_13_out, buffer_14_out,
       buffer_15_out, buffer_16_out;
  wire [15:0] buffer_5_out, buffer_6_out, buffer_7_out, buffer_8_out;
  wire [31:0] buffer_3_out, buffer_4_out;
  wire [63:0] adder_1_out, adder_3_out, adder_7_out, adder_15_out, and_3_out, bit_extender_1_out,
       bit_extender_2_out, bit_extender_3_out, bit_extender_4_out, bit_extender_5_out, bit_extender_6_out,
       bit_extender_7_out, bit_extender_8_out, bit_extender_9_out, buffer_1_out, buffer_2_out, counter_1_q,
       counter_2_q, divider_1_out, divider_1_rem, divider_3_out, divider_7_out, divider_15_out,
       fpadder_1_out, fpadder_3_out, fpadder_7_out, fpadder_15_out, fpdivider_1_out, fpdivider_3_out,
       fpdivider_7_out, fpdivider_15_out, fpexponentiator_1_p1, fplogarithm_1_p3, fpmultiplier_1_out,
       fpmultiplier_3_out, fpmultiplier_7_out, fpmultiplier_15_out, fpnegator_1_p2, fpnegator_3_p2,
       fpnegator_7_p2, fpnegator_15_p18, fpsquareroot_1_p1, fpsubtractor_1_out, fpsubtractor_3_out,
       fpsubtractor_7_out, fpsubtractor_15_out, fptoint_1_p1, fptoint_2_p1, fptoint_3_p1, fptoint_4_p1,
       fptrigonometry_1_p4, fptrigonometry_1_p5, fptrigonometry_1_p6, fptrigonometry_2_p2,
       fptrigonometry_2_p3, fptrigonometry_2_p4, inttofp_1_p1, multiplexer_1_out, multiplexer_2_out,
       multiplexer_3_out, multiplexer_4_out, multiplexer_5_out, multiplexer_6_out, multiplexer_7_out,
       multiplexer_8_out, multiplexer_9_out, multiplexer_10_out, multiplexer_11_out, multiplexer_12_out,
       multiplexer_13_out, multiplexer_14_out, multiplexer_15_out, multiplexer_16_out, multiplexer_17_out,
       multiplexer_18_out, multiplexer_19_out, multiplexer_20_out, multiplexer_21_out, multiplexer_22_out,
       multiplexer_24_out, multiplexer_26_out, multiplexer_27_out, multiplexer_28_out, multiplexer_29_out,
       multiplexer_31_out, multiplexer_33_out, multiplexer_35_out, multiplexer_37_out, multiplexer_41_out,
       multiplexer_45_out, multiplexer_49_out, multiplexer_53_out, multiplexer_57_out, multiplexer_65_out,
       multiplexer_73_out, multiplexer_81_out, multiplexer_89_out, multiplexer_97_out, multiplier_1_cout,
       multiplier_1_out, multiplier_3_out, multiplier_7_out, multiplier_15_out, nand_1_out, negator_1_out,
       negator_3_out, negator_7_out, negator_15_out, nor_1_out, not_2_out, or_1_out, register_1_q,
       shifter_1_out, shifter_2_out, shifter_3_out, shifter_4_out, shifter_5_out, shifter_7_out,
       shifter_9_out, shifter_11_out, shifter_13_out, shifter_15_out, shifter_19_out, shifter_23_out,
       shifter_27_out, shifter_31_out, shifter_35_out, shifter_43_out, shifter_51_out, shifter_59_out,
       shifter_67_out, shifter_75_out, subtractor_1_out, subtractor_3_out, subtractor_7_out,
       subtractor_15_out, undriven, xnor_1_out, xor_1_out;

  BitSelector #(.group(6), .width(64)) bitselector_1 (.in(argZ), .out(bitselector_1_out), .sel(4'b0000));
  Comparator #(.mode("unsigned"), .width(4)) comparator_1 (.a(op), .b(4'b0001), .eq(comparator_1_eq));  // open: gt, lt
  Comparator #(.width(64)) comparator_2 (
    .a(argY), .b({64{1'b0}}), .eq(comparator_2_eq), .lt(comparator_2_lt));  // open: gt
  // FPComparator #(.fpwidth(64)) fpcomparator_1: pin names not known; wires that end beside it: argX, argY, argZ, argY, {64{1'b0}}, fpcomparator_1_p6, fpcomparator_1_p7
  Comparator #(.mode("unsigned"), .width(4)) comparator_3 (.a(op), .b(4'b0010), .eq(comparator_3_eq));  // open: gt, lt
  Shifter #(.width(64)) shifter_1 (.in(argY), .\dist (bitselector_1_out), .out(shifter_1_out));
  Comparator #(.mode("unsigned"), .width(4)) comparator_4 (.a(op), .b(4'b0011), .eq(comparator_4_eq));  // open: gt, lt
  BitFinder #(.width(64)) bitfinder_1 (.in(argY), .index(bitfinder_1_index), .found(bitfinder_1_found));
  Comparator #(.mode("unsigned"), .width(4)) comparator_5 (.a(op), .b(4'b0100), .eq(comparator_5_eq));  // open: gt, lt
  Adder #(.width(64)) adder_1 (.a(argZ), .b(argY), .out(adder_1_out), .cout(adder_1_cout));  // open: cin
  assign bit_extender_1_out = {{63{1'b0}}, adder_1_cout};  // Bit_Extender bit_extender_1
  Comparator #(.mode("unsigned"), .width(4)) comparator_6 (.a(op), .b(4'b0101), .eq(comparator_6_eq));  // open: gt, lt
  FPAdder #(.fpwidth(64)) fpadder_1 (.a(argY), .b(argZ), .out(fpadder_1_out));
  Comparator #(.mode("unsigned"), .width(4)) comparator_7 (.a(op), .b(4'b0110), .eq(comparator_7_eq));  // open: gt, lt
  // FPTrigonometry #(.fpwidth(64)) fptrigonometry_1: pin names not known; wires that end beside it: argX, argY, argZ, fptrigonometry_1_p4, fptrigonometry_1_p5, fptrigonometry_1_p6
  Comparator #(.mode("unsigned"), .width(4)) comparator_8 (.a(op), .b(4'b0111), .eq(comparator_8_eq));  // open: gt, lt
  not not_1 (not_1_out, comparator_9_eq);
  Comparator #(.width(64)) comparator_9 (.a({64{1'b0}}), .b(argZ), .eq(comparator_9_eq));  // open: gt, lt
  Multiplexer #(.select(4), .width(64)) multiplexer_1 (
    .in0(multiplexer_2_out), .in1(multiplexer_10_out), .in2(multiplexer_11_out), .in3(multiplexer_12_out),
    .in4(multiplexer_14_out), .in5(multiplexer_15_out), .in6(multiplexer_16_out), .in7(multiplexer_19_out),
    .out(multiplexer_1_out), .sel(\var ));  // open: in8, in9, in10, in11, in12, in13, in14, in15
  Multiplexer #(.width(64)) multiplexer_2 (
    .in0({64{1'b0}}), .in1(64'h1), .out(multiplexer_2_out), .sel(comparator_2_eq));
  Multiplexer #(.select(4), .width(64)) multiplexer_3 (
    .in0(shifter_1_out), .in1(shifter_2_out), .in2(shifter_3_out), .in3(shifter_4_out), .in4(shifter_5_out),
    .in5(buffer_1_out), .in6(not_2_out), .in7(or_1_out), .in8(and_3_out), .in9(nand_1_out), .in10(nor_1_out),
    .in11(xor_1_out), .in12(xnor_1_out), .in13(multiplexer_20_out), .out(multiplexer_3_out), .sel(\var ));  // open: in14, in15
  Shifter #(.shift("lr"), .width(64)) shifter_2 (.in(argY), .\dist (bitselector_1_out), .out(shifter_2_out));
  Multiplexer #(.select(4), .width(64)) multiplexer_4 (
    .in0(multiplexer_5_out), .in1(multiplexer_13_out), .in2(multiplexer_17_out), .in3(multiplexer_21_out),
    .in4(bit_extender_7_out), .out(multiplexer_4_out), .sel(\var ));  // open: in5, in6, in7, in8, in9, in10, in11, in12, in13, in14, in15
  assign bit_extender_2_out = {{58{1'b0}}, bitfinder_1_index};  // Bit_Extender bit_extender_2
  Multiplexer #(.width(64)) multiplexer_5 (
    .in0({64{1'b1}}), .in1(bit_extender_2_out), .out(multiplexer_5_out), .sel(bitfinder_1_found));
  Multiplexer #(.select(4), .width(64)) multiplexer_6 (
    .in0(adder_1_out), .in1(bit_extender_1_out), .in2(subtractor_1_out), .in3(bit_extender_3_out),
    .in4(multiplier_1_out), .in5(multiplier_1_cout), .in6(divider_1_out), .in7(divider_1_rem),
    .in8(negator_1_out), .out(multiplexer_6_out), .sel(\var ));  // open: in9, in10, in11, in12, in13, in14, in15
  Subtractor #(.width(64)) subtractor_1 (
    .a(argY), .b(argZ), .out(subtractor_1_out), .bout(subtractor_1_bout));  // open: bin
  Multiplexer #(.select(4), .width(64)) multiplexer_7 (
    .in0(fpadder_1_out), .in1(fpsubtractor_1_out), .in2(fpmultiplier_1_out), .in3(fpdivider_1_out),
    .in4(fpnegator_1_p2), .in5(inttofp_1_p1), .in6(fptoint_1_p1), .in7(fptoint_2_p1), .in8(fptoint_3_p1),
    .in9(fptoint_4_p1), .in10(bit_extender_8_out), .in11(bit_extender_9_out), .out(multiplexer_7_out),
    .sel(\var ));  // open: in12, in13, in14, in15
  FPSubtractor #(.fpwidth(64)) fpsubtractor_1 (.a(argY), .b(argZ), .out(fpsubtractor_1_out));
  Multiplexer #(.select(4), .width(64)) multiplexer_8 (
    .in0(fptrigonometry_1_p4), .in1(fptrigonometry_1_p5), .in2(fptrigonometry_1_p6),
    .in3(fptrigonometry_2_p2), .in4(fptrigonometry_2_p3), .in5(fptrigonometry_2_p4), .in6(fplogarithm_1_p3),
    .in7(fpexponentiator_1_p1), .in8(fpsquareroot_1_p1), .out(multiplexer_8_out), .sel(\var ));  // open: in9, in10, in11, in12, in13, in14, in15
  // FPTrigonometry #(.fpwidth(64), .\type ("arc")) fptrigonometry_2: pin names not known; wires that end beside it: argY, fptrigonometry_2_p2, fptrigonometry_2_p3, fptrigonometry_2_p4
  Multiplexer #(.select(4), .width(64)) multiplexer_9 (
    .in0(counter_1_q), .in1(undriven), .in2(multiplexer_18_out), .in3(multiplexer_22_out), .in4(counter_2_q),
    .out(multiplexer_9_out), .sel(\var ));  // open: in5, in6, in7, in8, in9, in10, in11, in12, in13, in14, in15
  and and_1 (and_1_out, and_2_out, not_1_out);
  Clock clock_1 (.out(clock_1_out));
  Multiplexer #(.width(64)) multiplexer_10 (
    .in0({64{1'b0}}), .in1(64'h1), .out(multiplexer_10_out), .sel(comparator_2_lt));
  Multiplexer #(.width(64)) multiplexer_11 (
    .in0({64{1'b0}}), .in1(64'h1), .out(multiplexer_11_out), .sel(fpcomparator_1_p6));
  Shifter #(.shift("ar"), .width(64)) shifter_3 (.in(argY), .\dist (bitselector_1_out), .out(shifter_3_out));
  BitFinder #(.\type ("high1"), .width(64)) bitfinder_2 (
    .in(argY), .index(bitfinder_2_index), .found(bitfinder_2_found));
  assign bit_extender_3_out = {{63{1'b0}}, subtractor_1_bout};  // Bit_Extender bit_extender_3
  FPMultiplier #(.fpwidth(64)) fpmultiplier_1 (.a(argY), .b(argZ), .out(fpmultiplier_1_out));
  // FPLogarithm #(.fpwidth(64)) fplogarithm_1: pin names not known; wires that end beside it: argY, argZ, fplogarithm_1_p3, argY, argZ
  // Random #(.seed(12345667), .width(64)) random_1: pin names not known; wires that end beside it: random_1_p1
  Counter #(.max('hffffffffffffffff), .width(64)) counter_1 (
    .load(and_1_out), .D(argY), .Q(counter_1_q), .clk(clock_1_out));  // open: count, carry, up, clr
  Clock clock_2 (.out(random_1_p1));
  Multiplexer #(.width(64)) multiplexer_12 (
    .in0({64{1'b0}}), .in1(64'h1), .out(multiplexer_12_out), .sel(fpcomparator_1_p7));
  Shifter #(.shift("rl"), .width(64)) shifter_4 (.in(argY), .\dist (bitselector_1_out), .out(shifter_4_out));
  assign bit_extender_4_out = {{58{1'b0}}, bitfinder_2_index};  // Bit_Extender bit_extender_4
  Multiplier #(.mode("twosComplement"), .width(64)) multiplier_1 (
    .a(argY), .b(argZ), .out(multiplier_1_out), .cout(multiplier_1_cout));  // open: cin
  FPDivider #(.fpwidth(64)) fpdivider_1 (.a(argY), .b(argZ), .out(fpdivider_1_out));
  // FPExponentiator #(.fpwidth(64)) fpexponentiator_1: pin names not known; wires that end beside it: fpexponentiator_1_p1, argY
  Comparator #(.mode("unsigned"), .width(4)) comparator_10 (
    .a(\var ), .b(4'b0000), .eq(comparator_10_eq));  // open: gt, lt
  and and_2 (and_2_out, comparator_10_eq, comparator_8_eq);
  Comparator #(.width(64)) comparator_11 (
    .a(argY), .b(argZ), .eq(comparator_11_eq), .lt(comparator_11_lt));  // open: gt
  // FPComparator #(.fpwidth(64)) fpcomparator_2: pin names not known; wires that end beside it: argY, argZ, fpcomparator_2_p3, fpcomparator_2_p4
  assign not_2_out = ~argY;  // NOT_Gate not_2, 64 bits wide
  assign buffer_1_out = argY;  // Buffer buffer_1, 64 bits wide
  Shifter #(.shift("rr"), .width(64)) shifter_5 (.in(argY), .\dist (bitselector_1_out), .out(shifter_5_out));
  Multiplexer #(.width(64)) multiplexer_13 (
    .in0({64{1'b1}}), .in1(bit_extender_4_out), .out(multiplexer_13_out), .sel(bitfinder_2_found));
  Divider #(.mode("twosComplement"), .width(64)) divider_1 (
    .a(argY), .b(argZ), .out(divider_1_out), .rem(divider_1_rem));  // open: upper
  // FPNegator #(.fpwidth(64)) fpnegator_1: pin names not known; wires that end beside it: argY, fpnegator_1_p2, argY
  // IntToFP #(.fpwidth(64), .width(64)) inttofp_1: pin names not known; wires that end beside it: inttofp_1_p1, argY
  // FPSquareRoot #(.fpwidth(64)) fpsquareroot_1: pin names not known; wires that end beside it: fpsquareroot_1_p1
  Comparator #(.mode("unsigned"), .width(4)) comparator_12 (
    .a(\var ), .b(4'b0010), .eq(comparator_12_eq));  // open: gt, lt
  not not_3 (not_3_out, comparator_13_eq);
  Comparator #(.width(64)) comparator_13 (.a({64{1'b0}}), .b(argZ), .eq(comparator_13_eq));  // open: gt, lt
  Multiplexer #(.width(64)) multiplexer_14 (
    .in0({64{1'b0}}), .in1(64'h1), .out(multiplexer_14_out), .sel(comparator_11_eq));
  Multiplexer #(.width(64)) multiplexer_15 (
    .in0({64{1'b0}}), .in1(64'h1), .out(multiplexer_15_out), .sel(comparator_11_lt));
  assign nand_1_out = ~(argY & argZ);  // NAND_Gate nand_1, 64 bits wide
  assign or_1_out = argY | argZ;  // OR_Gate or_1, 64 bits wide
  assign and_3_out = argY & argZ;  // AND_Gate and_3, 64 bits wide
  assign bit_extender_5_out = {{58{1'b0}}, bitfinder_3_index};  // Bit_Extender bit_extender_5
  BitFinder #(.\type ("low0"), .width(64)) bitfinder_3 (
    .in(argY), .index(bitfinder_3_index), .found(bitfinder_3_found));
  Negator #(.width(64)) negator_1 (.in(argY), .out(negator_1_out));
  // FPToInt #(.fpwidth(64), .width(64)) fptoint_1: pin names not known; wires that end beside it: fptoint_1_p1, argY
  and and_4 (and_4_out, comparator_12_eq, comparator_8_eq);
  Register #(.width(64)) register_1 (.D(argY), .en(and_5_out), .clk(clock_3_out), .Q(register_1_q));  // open: clr
  and and_5 (and_5_out, and_4_out, not_3_out);
  Clock clock_3 (.out(clock_3_out));
  Multiplexer #(.width(64)) multiplexer_16 (
    .in0({64{1'b0}}), .in1(64'h1), .out(multiplexer_16_out), .sel(fpcomparator_2_p3));
  assign nor_1_out = ~(argY | argZ);  // NOR_Gate nor_1, 64 bits wide
  assign xor_1_out = argY ^ argZ;  // XOR_Gate xor_1, 64 bits wide
  Multiplexer #(.width(64)) multiplexer_17 (
    .in0({64{1'b1}}), .in1(bit_extender_5_out), .out(multiplexer_17_out), .sel(bitfinder_3_found));
  // FPToInt #(.fpwidth(64), .mode("floor"), .width(64)) fptoint_2: pin names not known; wires that end beside it: fptoint_2_p1, argY
  Multiplexer #(.width(64)) multiplexer_18 (
    .in0(register_1_q), .in1(64'h12a05f200), .out(multiplexer_18_out), .sel(comparator_14_eq));
  Comparator #(.width(64)) comparator_14 (.a({64{1'b0}}), .b(register_1_q), .eq(comparator_14_eq));  // open: gt, lt
  Multiplexer #(.width(64)) multiplexer_19 (
    .in0({64{1'b0}}), .in1(64'h1), .out(multiplexer_19_out), .sel(fpcomparator_2_p4));
  assign xnor_1_out = ~(argY ^ argZ);  // XNOR_Gate xnor_1, 64 bits wide
  BitFinder #(.\type ("high0"), .width(64)) bitfinder_4 (
    .in(argY), .index(bitfinder_4_index), .found(bitfinder_4_found));
  // FPToInt #(.fpwidth(64), .mode("ceil"), .width(64)) fptoint_3: pin names not known; wires that end beside it: fptoint_3_p1, argY
  Multiplexer #(.width(64)) multiplexer_20 (.in0(argX), .in1(buffer_2_out), .out(multiplexer_20_out), .sel(not_4_out));
  assign buffer_2_out = argY;  // Buffer buffer_2, 64 bits wide
  not not_4 (not_4_out, comparator_15_eq);
  Comparator #(.mode("unsigned"), .width(64)) comparator_15 (
    .a(argZ), .b({64{1'b0}}), .eq(comparator_15_eq));  // open: gt, lt
  assign bit_extender_6_out = {{58{1'b0}}, bitfinder_4_index};  // Bit_Extender bit_extender_6
  Multiplexer #(.width(64)) multiplexer_21 (
    .in0({64{1'b1}}), .in1(bit_extender_6_out), .out(multiplexer_21_out), .sel(bitfinder_4_found));
  // FPToInt #(.fpwidth(64), .mode("truncate"), .width(64)) fptoint_4: pin names not known; wires that end beside it: fptoint_4_p1, argY
  BitSelector #(.group(3), .width(64)) bitselector_2 (.in(argY), .out(bitselector_2_out), .sel({5{1'b0}}));
  BitAdder #(.width(64)) bitadder_1 (.in0(argY), .out(bitadder_1_out));
  // FPClassificator #(.fpwidth(64)) fpclassificator_1: pin names not known; wires that end beside it: fpclassificator_1_p1, fpclassificator_1_p2
  Multiplexer #(.select(3), .width(64)) multiplexer_22 (
    .in0({64{1'b0}}), .in1(64'h1), .in2(64'h65536), .in3(64'h1000000), .in4(64'h200), .in5(64'h200),
    .in6({64{1'b0}}), .in7({64{1'b0}}), .out(multiplexer_22_out), .sel(bitselector_2_out));
  assign bit_extender_7_out = {{57{1'b0}}, bitadder_1_out};  // Bit_Extender bit_extender_7
  assign bit_extender_8_out = {{63{1'b0}}, fpclassificator_1_p1};  // Bit_Extender bit_extender_8
  assign bit_extender_9_out = {{63{1'b0}}, fpclassificator_1_p2};  // Bit_Extender bit_extender_9
  not not_5 (not_5_out, comparator_16_eq);
  Comparator #(.width(64)) comparator_16 (.a({64{1'b0}}), .b(argZ), .eq(comparator_16_eq));  // open: gt, lt
  Comparator #(.mode("unsigned"), .width(4)) comparator_17 (
    .a(\var ), .b(4'b0100), .eq(comparator_17_eq));  // open: gt, lt
  and and_6 (and_6_out, comparator_17_eq, comparator_8_eq);
  and and_7 (and_7_out, and_6_out, not_5_out);
  Clock #(.lowDuration(9)) clock_4 (.out(clock_4_out));
  Counter #(.max('hffffffffffffffff), .width(64)) counter_2 (
    .load(and_7_out), .D(argY), .Q(counter_2_q), .clk(clock_4_out));  // open: count, carry, up, clr
  or or_2 (we, comparator_1_eq, comparator_3_eq, comparator_4_eq, comparator_5_eq, comparator_6_eq, comparator_7_eq, comparator_8_eq, comparator_18_eq, comparator_19_eq, comparator_20_eq, comparator_21_eq);
  Multiplexer #(.select(4), .width(64)) multiplexer_23 (
    .in1(multiplexer_1_out), .in2(multiplexer_3_out), .in3(multiplexer_4_out), .in4(multiplexer_6_out),
    .in5(multiplexer_7_out), .in6(multiplexer_8_out), .in7(multiplexer_9_out), .in8(multiplexer_24_out),
    .in9(multiplexer_26_out), .in10(multiplexer_27_out), .in11(multiplexer_28_out), .out(outX), .sel(op));  // open: in0, in12, in13, in14, in15
  Comparator #(.mode("unsigned"), .width(4)) comparator_18 (
    .a(op), .b(4'b1000), .eq(comparator_18_eq));  // open: gt, lt
  Comparator #(.mode("unsigned"), .width(4)) comparator_19 (
    .a(op), .b(4'b1001), .eq(comparator_19_eq));  // open: gt, lt
  Comparator #(.mode("unsigned"), .width(4)) comparator_20 (
    .a(op), .b(4'b1010), .eq(comparator_20_eq));  // open: gt, lt
  Comparator #(.mode("unsigned"), .width(4)) comparator_21 (
    .a(op), .b(4'b1011), .eq(comparator_21_eq));  // open: gt, lt
  BitSelector #(.group(5), .width(32)) bitselector_3 (.in(argZ[31:0]), .out(bitselector_3_out), .sel(3'b000));
  BitSelector #(.group(5), .width(32)) bitselector_4 (.in(argZ[63:32]), .out(bitselector_4_out), .sel(3'b000));
  Multiplexer #(.select(4), .width(64)) multiplexer_24 (
    .in0(multiplexer_29_out), .in1(multiplexer_31_out), .in2(multiplexer_33_out), .in3(multiplexer_35_out),
    .in4(multiplexer_37_out), .in5(multiplexer_41_out), .in6(multiplexer_45_out), .in7(multiplexer_49_out),
    .in8(multiplexer_53_out), .in9(multiplexer_57_out), .in10(multiplexer_65_out), .in11(multiplexer_73_out),
    .in12(multiplexer_81_out), .in13(multiplexer_89_out), .in14(multiplexer_97_out),
    .out(multiplexer_24_out), .sel(\var ));  // open: in15
  Multiplexer #(.width(32)) multiplexer_25 (
    .in0({32{1'b0}}), .in1(32'h1), .out(multiplexer_29_out[63:32]), .sel(comparator_22_eq));
  Comparator #(.width(32)) comparator_22 (
    .a(argY[63:32]), .b({32{1'b0}}), .eq(comparator_22_eq), .lt(comparator_22_lt));  // open: gt
  Comparator #(.width(32)) comparator_23 (
    .a(argY[31:0]), .b({32{1'b0}}), .eq(comparator_23_eq), .lt(comparator_23_lt));  // open: gt
  Multiplexer #(.select(4), .width(64)) multiplexer_26 (
    .in0(shifter_7_out), .in1(shifter_9_out), .in2(shifter_11_out), .in3(shifter_13_out),
    .in4(shifter_15_out), .in5(shifter_19_out), .in6(shifter_23_out), .in7(shifter_27_out),
    .in8(shifter_31_out), .in9(shifter_35_out), .in10(shifter_43_out), .in11(shifter_51_out),
    .in12(shifter_59_out), .in13(shifter_67_out), .in14(shifter_75_out), .out(multiplexer_26_out), .sel(\var ));  // open: in15
  Shifter #(.width(32)) shifter_6 (.in(argY[63:32]), .\dist (bitselector_4_out), .out(shifter_7_out[63:32]));
  Shifter #(.width(32)) shifter_7 (.in(argY[31:0]), .\dist (bitselector_3_out), .out(shifter_7_out[31:0]));
  Multiplexer #(.select(4), .width(64)) multiplexer_27 (
    .in0(adder_3_out), .in1(subtractor_3_out), .in2(multiplier_3_out), .in3(divider_3_out),
    .in4(negator_3_out), .in5(adder_7_out), .in6(subtractor_7_out), .in7(multiplier_7_out),
    .in8(divider_7_out), .in9(negator_7_out), .in10(adder_15_out), .in11(subtractor_15_out),
    .in12(multiplier_15_out), .in13(divider_15_out), .in14(negator_15_out), .out(multiplexer_27_out),
    .sel(\var ));  // open: in15
  Adder #(.width(32)) adder_2 (.a(argY[63:32]), .b(argZ[63:32]), .out(adder_3_out[63:32]));  // open: cin, cout
  Adder #(.width(32)) adder_3 (.a(argY[31:0]), .b(argZ[31:0]), .out(adder_3_out[31:0]));  // open: cin, cout
  Multiplexer #(.select(4), .width(64)) multiplexer_28 (
    .in0(fpadder_3_out), .in1(fpsubtractor_3_out), .in2(fpmultiplier_3_out), .in3(fpdivider_3_out),
    .in4(fpnegator_3_p2), .in5(fpadder_7_out), .in6(fpsubtractor_7_out), .in7(fpmultiplier_7_out),
    .in8(fpdivider_7_out), .in9(fpnegator_7_p2), .in10(fpadder_15_out), .in11(fpsubtractor_15_out),
    .in12(fpmultiplier_15_out), .in13(fpdivider_15_out), .in14(fpnegator_15_p18), .out(multiplexer_28_out),
    .sel(\var ));  // open: in15
  FPAdder fpadder_2 (.a(argY[63:32]), .b(argZ[63:32]), .out(fpadder_3_out[63:32]));
  FPAdder fpadder_3 (.a(argY[31:0]), .b(argZ[31:0]), .out(fpadder_3_out[31:0]));
  Multiplexer #(.width(32)) multiplexer_29 (
    .in0({32{1'b0}}), .in1(32'h1), .out(multiplexer_29_out[31:0]), .sel(comparator_23_eq));
  Shifter #(.shift("lr"), .width(32)) shifter_8 (
    .in(argY[63:32]), .\dist (bitselector_4_out), .out(shifter_9_out[63:32]));
  Shifter #(.shift("lr"), .width(32)) shifter_9 (
    .in(argY[31:0]), .\dist (bitselector_3_out), .out(shifter_9_out[31:0]));
  Subtractor #(.width(32)) subtractor_2 (
    .a(argY[63:32]), .b(argZ[63:32]), .out(subtractor_3_out[63:32]));  // open: bin, bout
  Subtractor #(.width(32)) subtractor_3 (
    .a(argY[31:0]), .b(argZ[31:0]), .out(subtractor_3_out[31:0]));  // open: bin, bout
  FPSubtractor fpsubtractor_2 (.a(argY[63:32]), .b(argZ[63:32]), .out(fpsubtractor_3_out[63:32]));
  FPSubtractor fpsubtractor_3 (.a(argY[31:0]), .b(argZ[31:0]), .out(fpsubtractor_3_out[31:0]));
  Multiplexer #(.width(32)) multiplexer_30 (
    .in0({32{1'b0}}), .in1(32'h1), .out(multiplexer_31_out[63:32]), .sel(comparator_22_lt));
  Multiplexer #(.width(32)) multiplexer_31 (
    .in0({32{1'b0}}), .in1(32'h1), .out(multiplexer_31_out[31:0]), .sel(comparator_23_lt));
  Shifter #(.shift("ar"), .width(32)) shifter_10 (
    .in(argY[63:32]), .\dist (bitselector_4_out), .out(shifter_11_out[63:32]));
  Shifter #(.shift("ar"), .width(32)) shifter_11 (
    .in(argY[31:0]), .\dist (bitselector_3_out), .out(shifter_11_out[31:0]));
  Multiplier #(.mode("twosComplement"), .width(32)) multiplier_2 (
    .a(argY[63:32]), .b(argZ[63:32]), .out(multiplier_3_out[63:32]));  // open: cin, cout
  Multiplier #(.mode("twosComplement"), .width(32)) multiplier_3 (
    .a(argY[31:0]), .b(argZ[31:0]), .out(multiplier_3_out[31:0]));  // open: cin, cout
  FPMultiplier fpmultiplier_2 (.a(argY[63:32]), .b(argZ[63:32]), .out(fpmultiplier_3_out[63:32]));
  FPMultiplier fpmultiplier_3 (.a(argY[31:0]), .b(argZ[31:0]), .out(fpmultiplier_3_out[31:0]));
  Multiplexer #(.width(32)) multiplexer_32 (
    .in0({32{1'b0}}), .in1(32'h1), .out(multiplexer_33_out[63:32]), .sel(fpcomparator_3_p3));
  // FPComparator fpcomparator_3: pin names not known; wires that end beside it: argY[63:32], {32{1'b0}}, fpcomparator_3_p3, fpcomparator_3_p4
  // FPComparator fpcomparator_4: pin names not known; wires that end beside it: argY[31:0], {32{1'b0}}, fpcomparator_4_p3, fpcomparator_4_p4
  Shifter #(.shift("rl"), .width(32)) shifter_12 (
    .in(argY[63:32]), .\dist (bitselector_4_out), .out(shifter_13_out[63:32]));
  Shifter #(.shift("rl"), .width(32)) shifter_13 (
    .in(argY[31:0]), .\dist (bitselector_3_out), .out(shifter_13_out[31:0]));
  Divider #(.mode("twosComplement"), .width(32)) divider_2 (
    .a(argY[63:32]), .b(argZ[63:32]), .out(divider_3_out[63:32]));  // open: upper, rem
  Divider #(.mode("twosComplement"), .width(32)) divider_3 (
    .a(argY[31:0]), .b(argZ[31:0]), .out(divider_3_out[31:0]));  // open: upper, rem
  FPDivider fpdivider_2 (.a(argY[63:32]), .b(argZ[63:32]), .out(fpdivider_3_out[63:32]));
  FPDivider fpdivider_3 (.a(argY[31:0]), .b(argZ[31:0]), .out(fpdivider_3_out[31:0]));
  Multiplexer #(.width(32)) multiplexer_33 (
    .in0({32{1'b0}}), .in1(32'h1), .out(multiplexer_33_out[31:0]), .sel(fpcomparator_4_p3));
  Shifter #(.shift("rr"), .width(32)) shifter_14 (
    .in(argY[63:32]), .\dist (bitselector_4_out), .out(shifter_15_out[63:32]));
  Shifter #(.shift("rr"), .width(32)) shifter_15 (
    .in(argY[31:0]), .\dist (bitselector_3_out), .out(shifter_15_out[31:0]));
  Negator #(.width(32)) negator_2 (.in(argY[63:32]), .out(negator_3_out[63:32]));
  Negator #(.width(32)) negator_3 (.in(argY[31:0]), .out(negator_3_out[31:0]));
  // FPNegator fpnegator_2: pin names not known; wires that end beside it: argY[63:32], fpnegator_3_p2[63:32]
  // FPNegator fpnegator_3: pin names not known; wires that end beside it: argY[31:0], fpnegator_3_p2[31:0]
  Multiplexer #(.width(32)) multiplexer_34 (
    .in0({32{1'b0}}), .in1(32'h1), .out(multiplexer_35_out[63:32]), .sel(fpcomparator_3_p4));
  Multiplexer #(.width(32)) multiplexer_35 (
    .in0({32{1'b0}}), .in1(32'h1), .out(multiplexer_35_out[31:0]), .sel(fpcomparator_4_p4));
  BitSelector #(.group(4), .width(16)) bitselector_5 (.in(argZ[15:0]), .out(bitselector_5_out), .sel(2'b00));
  BitSelector #(.group(4), .width(16)) bitselector_6 (.in(argZ[31:16]), .out(bitselector_6_out), .sel(2'b00));
  BitSelector #(.group(4), .width(16)) bitselector_7 (.in(argZ[47:32]), .out(bitselector_7_out), .sel(2'b00));
  BitSelector #(.group(4), .width(16)) bitselector_8 (.in(argZ[63:48]), .out(bitselector_8_out), .sel(2'b00));
  Multiplexer #(.width(32)) multiplexer_36 (
    .in0(argX[63:32]), .in1(buffer_3_out), .out(multiplexer_37_out[63:32]), .sel(not_6_out));
  assign buffer_3_out = argY[63:32];  // Buffer buffer_3, 32 bits wide
  Adder #(.width(16)) adder_4 (.a(argY[63:48]), .b(argZ[63:48]), .out(adder_7_out[63:48]));  // open: cin, cout
  Adder #(.width(16)) adder_5 (.a(argY[47:32]), .b(argZ[47:32]), .out(adder_7_out[47:32]));  // open: cin, cout
  Adder #(.width(16)) adder_6 (.a(argY[31:16]), .b(argZ[31:16]), .out(adder_7_out[31:16]));  // open: cin, cout
  Adder #(.width(16)) adder_7 (.a(argY[15:0]), .b(argZ[15:0]), .out(adder_7_out[15:0]));  // open: cin, cout
  FPAdder #(.fpwidth(16)) fpadder_4 (.a(argY[63:48]), .b(argZ[63:48]), .out(fpadder_7_out[63:48]));
  FPAdder #(.fpwidth(16)) fpadder_5 (.a(argY[47:32]), .b(argZ[47:32]), .out(fpadder_7_out[47:32]));
  FPAdder #(.fpwidth(16)) fpadder_6 (.a(argY[31:16]), .b(argZ[31:16]), .out(fpadder_7_out[31:16]));
  FPAdder #(.fpwidth(16)) fpadder_7 (.a(argY[15:0]), .b(argZ[15:0]), .out(fpadder_7_out[15:0]));
  Multiplexer #(.width(32)) multiplexer_37 (
    .in0(argX[31:0]), .in1(buffer_4_out), .out(multiplexer_37_out[31:0]), .sel(not_7_out));
  assign buffer_4_out = argY[31:0];  // Buffer buffer_4, 32 bits wide
  not not_6 (not_6_out, comparator_24_eq);
  Comparator #(.mode("unsigned"), .width(32)) comparator_24 (
    .a(argZ[63:32]), .b({32{1'b0}}), .eq(comparator_24_eq));  // open: gt, lt
  not not_7 (not_7_out, comparator_25_eq);
  Comparator #(.mode("unsigned"), .width(32)) comparator_25 (
    .a(argZ[31:0]), .b({32{1'b0}}), .eq(comparator_25_eq));  // open: gt, lt
  Shifter #(.width(16)) shifter_16 (.in(argY[63:48]), .\dist (bitselector_8_out), .out(shifter_19_out[63:48]));
  Shifter #(.width(16)) shifter_17 (.in(argY[47:32]), .\dist (bitselector_7_out), .out(shifter_19_out[47:32]));
  Shifter #(.width(16)) shifter_18 (.in(argY[31:16]), .\dist (bitselector_6_out), .out(shifter_19_out[31:16]));
  Shifter #(.width(16)) shifter_19 (.in(argY[15:0]), .\dist (bitselector_5_out), .out(shifter_19_out[15:0]));
  Subtractor #(.width(16)) subtractor_4 (
    .a(argY[63:48]), .b(argZ[63:48]), .out(subtractor_7_out[63:48]));  // open: bin, bout
  Subtractor #(.width(16)) subtractor_5 (
    .a(argY[47:32]), .b(argZ[47:32]), .out(subtractor_7_out[47:32]));  // open: bin, bout
  Subtractor #(.width(16)) subtractor_6 (
    .a(argY[31:16]), .b(argZ[31:16]), .out(subtractor_7_out[31:16]));  // open: bin, bout
  Subtractor #(.width(16)) subtractor_7 (
    .a(argY[15:0]), .b(argZ[15:0]), .out(subtractor_7_out[15:0]));  // open: bin, bout
  FPSubtractor #(.fpwidth(16)) fpsubtractor_4 (.a(argY[63:48]), .b(argZ[63:48]), .out(fpsubtractor_7_out[63:48]));
  FPSubtractor #(.fpwidth(16)) fpsubtractor_5 (.a(argY[47:32]), .b(argZ[47:32]), .out(fpsubtractor_7_out[47:32]));
  FPSubtractor #(.fpwidth(16)) fpsubtractor_6 (.a(argY[31:16]), .b(argZ[31:16]), .out(fpsubtractor_7_out[31:16]));
  FPSubtractor #(.fpwidth(16)) fpsubtractor_7 (.a(argY[15:0]), .b(argZ[15:0]), .out(fpsubtractor_7_out[15:0]));
  Shifter #(.shift("lr"), .width(16)) shifter_20 (
    .in(argY[63:48]), .\dist (bitselector_8_out), .out(shifter_23_out[63:48]));
  Shifter #(.shift("lr"), .width(16)) shifter_21 (
    .in(argY[47:32]), .\dist (bitselector_7_out), .out(shifter_23_out[47:32]));
  Shifter #(.shift("lr"), .width(16)) shifter_22 (
    .in(argY[31:16]), .\dist (bitselector_6_out), .out(shifter_23_out[31:16]));
  Shifter #(.shift("lr"), .width(16)) shifter_23 (
    .in(argY[15:0]), .\dist (bitselector_5_out), .out(shifter_23_out[15:0]));
  Multiplexer #(.width(16)) multiplexer_38 (
    .in0({16{1'b0}}), .in1(16'h1), .out(multiplexer_41_out[63:48]), .sel(comparator_26_eq));
  Comparator #(.width(16)) comparator_26 (
    .a(argY[63:48]), .b({16{1'b0}}), .eq(comparator_26_eq), .lt(comparator_26_lt));  // open: gt
  Comparator #(.width(16)) comparator_27 (
    .a(argY[47:32]), .b({16{1'b0}}), .eq(comparator_27_eq), .lt(comparator_27_lt));  // open: gt
  Comparator #(.width(16)) comparator_28 (
    .a(argY[31:16]), .b({16{1'b0}}), .eq(comparator_28_eq), .lt(comparator_28_lt));  // open: gt
  Comparator #(.width(16)) comparator_29 (
    .a(argY[15:0]), .b({16{1'b0}}), .eq(comparator_29_eq), .lt(comparator_29_lt));  // open: gt
  Multiplexer #(.width(16)) multiplexer_39 (
    .in0({16{1'b0}}), .in1(16'h1), .out(multiplexer_41_out[47:32]), .sel(comparator_27_eq));
  Multiplier #(.mode("twosComplement"), .width(16)) multiplier_4 (
    .a(argY[63:48]), .b(argZ[63:48]), .out(multiplier_7_out[63:48]));  // open: cin, cout
  Multiplier #(.mode("twosComplement"), .width(16)) multiplier_5 (
    .a(argY[47:32]), .b(argZ[47:32]), .out(multiplier_7_out[47:32]));  // open: cin, cout
  Multiplier #(.mode("twosComplement"), .width(16)) multiplier_6 (
    .a(argY[31:16]), .b(argZ[31:16]), .out(multiplier_7_out[31:16]));  // open: cin, cout
  Multiplier #(.mode("twosComplement"), .width(16)) multiplier_7 (
    .a(argY[15:0]), .b(argZ[15:0]), .out(multiplier_7_out[15:0]));  // open: cin, cout
  FPMultiplier #(.fpwidth(16)) fpmultiplier_4 (.a(argY[63:48]), .b(argZ[63:48]), .out(fpmultiplier_7_out[63:48]));
  FPMultiplier #(.fpwidth(16)) fpmultiplier_5 (.a(argY[47:32]), .b(argZ[47:32]), .out(fpmultiplier_7_out[47:32]));
  FPMultiplier #(.fpwidth(16)) fpmultiplier_6 (.a(argY[31:16]), .b(argZ[31:16]), .out(fpmultiplier_7_out[31:16]));
  FPMultiplier #(.fpwidth(16)) fpmultiplier_7 (.a(argY[15:0]), .b(argZ[15:0]), .out(fpmultiplier_7_out[15:0]));
  Multiplexer #(.width(16)) multiplexer_40 (
    .in0({16{1'b0}}), .in1(16'h1), .out(multiplexer_41_out[31:16]), .sel(comparator_28_eq));
  Shifter #(.shift("ar"), .width(16)) shifter_24 (
    .in(argY[63:48]), .\dist (bitselector_8_out), .out(shifter_27_out[63:48]));
  Shifter #(.shift("ar"), .width(16)) shifter_25 (
    .in(argY[47:32]), .\dist (bitselector_7_out), .out(shifter_27_out[47:32]));
  Shifter #(.shift("ar"), .width(16)) shifter_26 (
    .in(argY[31:16]), .\dist (bitselector_6_out), .out(shifter_27_out[31:16]));
  Shifter #(.shift("ar"), .width(16)) shifter_27 (
    .in(argY[15:0]), .\dist (bitselector_5_out), .out(shifter_27_out[15:0]));
  Multiplexer #(.width(16)) multiplexer_41 (
    .in0({16{1'b0}}), .in1(16'h1), .out(multiplexer_41_out[15:0]), .sel(comparator_29_eq));
  Multiplexer #(.width(16)) multiplexer_42 (
    .in0({16{1'b0}}), .in1(16'h1), .out(multiplexer_45_out[63:48]), .sel(comparator_26_lt));
  Divider #(.mode("twosComplement"), .width(16)) divider_4 (
    .a(argY[63:48]), .b(argZ[63:48]), .out(divider_7_out[63:48]));  // open: upper, rem
  Divider #(.mode("twosComplement"), .width(16)) divider_5 (
    .a(argY[47:32]), .b(argZ[47:32]), .out(divider_7_out[47:32]));  // open: upper, rem
  Divider #(.mode("twosComplement"), .width(16)) divider_6 (
    .a(argY[31:16]), .b(argZ[31:16]), .out(divider_7_out[31:16]));  // open: upper, rem
  Divider #(.mode("twosComplement"), .width(16)) divider_7 (
    .a(argY[15:0]), .b(argZ[15:0]), .out(divider_7_out[15:0]));  // open: upper, rem
  FPDivider #(.fpwidth(16)) fpdivider_4 (.a(argY[63:48]), .b(argZ[63:48]), .out(fpdivider_7_out[63:48]));
  FPDivider #(.fpwidth(16)) fpdivider_5 (.a(argY[47:32]), .b(argZ[47:32]), .out(fpdivider_7_out[47:32]));
  FPDivider #(.fpwidth(16)) fpdivider_6 (.a(argY[31:16]), .b(argZ[31:16]), .out(fpdivider_7_out[31:16]));
  FPDivider #(.fpwidth(16)) fpdivider_7 (.a(argY[15:0]), .b(argZ[15:0]), .out(fpdivider_7_out[15:0]));
  Multiplexer #(.width(16)) multiplexer_43 (
    .in0({16{1'b0}}), .in1(16'h1), .out(multiplexer_45_out[47:32]), .sel(comparator_27_lt));
  Shifter #(.shift("rl"), .width(16)) shifter_28 (
    .in(argY[63:48]), .\dist (bitselector_8_out), .out(shifter_31_out[63:48]));
  Shifter #(.shift("rl"), .width(16)) shifter_29 (
    .in(argY[47:32]), .\dist (bitselector_7_out), .out(shifter_31_out[47:32]));
  Shifter #(.shift("rl"), .width(16)) shifter_30 (
    .in(argY[31:16]), .\dist (bitselector_6_out), .out(shifter_31_out[31:16]));
  Shifter #(.shift("rl"), .width(16)) shifter_31 (
    .in(argY[15:0]), .\dist (bitselector_5_out), .out(shifter_31_out[15:0]));
  Multiplexer #(.width(16)) multiplexer_44 (
    .in0({16{1'b0}}), .in1(16'h1), .out(multiplexer_45_out[31:16]), .sel(comparator_28_lt));
  Negator #(.width(16)) negator_4 (.in(argY[63:48]), .out(negator_7_out[63:48]));
  Negator #(.width(16)) negator_5 (.in(argY[47:32]), .out(negator_7_out[47:32]));
  Negator #(.width(16)) negator_6 (.in(argY[31:16]), .out(negator_7_out[31:16]));
  Negator #(.width(16)) negator_7 (.in(argY[15:0]), .out(negator_7_out[15:0]));
  // FPNegator #(.fpwidth(16)) fpnegator_4: pin names not known; wires that end beside it: argY[63:48], fpnegator_7_p2[63:48]
  // FPNegator #(.fpwidth(16)) fpnegator_5: pin names not known; wires that end beside it: argY[47:32], fpnegator_7_p2[47:32]
  // FPNegator #(.fpwidth(16)) fpnegator_6: pin names not known; wires that end beside it: argY[31:16], fpnegator_7_p2[31:16]
  // FPNegator #(.fpwidth(16)) fpnegator_7: pin names not known; wires that end beside it: argY[15:0], fpnegator_7_p2[15:0], argY[15:0], argY[31:16], argY[47:32], argY[63:48], argZ[15:0], argZ[31:16], argZ[47:32], argZ[63:48]
  Multiplexer #(.width(16)) multiplexer_45 (
    .in0({16{1'b0}}), .in1(16'h1), .out(multiplexer_45_out[15:0]), .sel(comparator_29_lt));
  Shifter #(.shift("rr"), .width(16)) shifter_32 (
    .in(argY[63:48]), .\dist (bitselector_8_out), .out(shifter_35_out[63:48]));
  Shifter #(.shift("rr"), .width(16)) shifter_33 (
    .in(argY[47:32]), .\dist (bitselector_7_out), .out(shifter_35_out[47:32]));
  Shifter #(.shift("rr"), .width(16)) shifter_34 (
    .in(argY[31:16]), .\dist (bitselector_6_out), .out(shifter_35_out[31:16]));
  Shifter #(.shift("rr"), .width(16)) shifter_35 (
    .in(argY[15:0]), .\dist (bitselector_5_out), .out(shifter_35_out[15:0]));
  Multiplexer #(.width(16)) multiplexer_46 (
    .in0({16{1'b0}}), .in1(16'h1), .out(multiplexer_49_out[63:48]), .sel(fpcomparator_5_p3));
  // FPComparator #(.fpwidth(16)) fpcomparator_5: pin names not known; wires that end beside it: argY[63:48], {16{1'b0}}, fpcomparator_5_p3, fpcomparator_5_p4
  // FPComparator #(.fpwidth(16)) fpcomparator_6: pin names not known; wires that end beside it: argY[47:32], {16{1'b0}}, fpcomparator_6_p3, fpcomparator_6_p4
  // FPComparator #(.fpwidth(16)) fpcomparator_7: pin names not known; wires that end beside it: argY[31:16], {16{1'b0}}, fpcomparator_7_p3, fpcomparator_7_p4
  // FPComparator #(.fpwidth(16)) fpcomparator_8: pin names not known; wires that end beside it: argY[15:0], {16{1'b0}}, fpcomparator_8_p3, fpcomparator_8_p4
  Multiplexer #(.width(16)) multiplexer_47 (
    .in0({16{1'b0}}), .in1(16'h1), .out(multiplexer_49_out[47:32]), .sel(fpcomparator_6_p3));
  Multiplexer #(.width(16)) multiplexer_48 (
    .in0({16{1'b0}}), .in1(16'h1), .out(multiplexer_49_out[31:16]), .sel(fpcomparator_7_p3));
  BitSelector #(.group(3)) bitselector_9 (.in(argZ[7:0]), .out(bitselector_9_out), .sel(2'b00));
  BitSelector #(.group(3)) bitselector_10 (.in(argZ[15:8]), .out(bitselector_10_out), .sel(2'b00));
  BitSelector #(.group(3)) bitselector_11 (.in(argZ[23:16]), .out(bitselector_11_out), .sel(2'b00));
  BitSelector #(.group(3)) bitselector_12 (.in(argZ[31:24]), .out(bitselector_12_out), .sel(2'b00));
  BitSelector #(.group(3)) bitselector_13 (.in(argZ[39:32]), .out(bitselector_13_out), .sel(2'b00));
  BitSelector #(.group(3)) bitselector_14 (.in(argZ[47:40]), .out(bitselector_14_out), .sel(2'b00));
  BitSelector #(.group(3)) bitselector_15 (.in(argZ[55:48]), .out(bitselector_15_out), .sel(2'b00));
  BitSelector #(.group(3)) bitselector_16 (.in(argZ[63:56]), .out(bitselector_16_out), .sel(2'b00));
  Adder adder_8 (.a(argY[63:56]), .b(argZ[63:56]), .out(adder_15_out[63:56]));  // open: cin, cout
  Adder adder_9 (.a(argY[55:48]), .b(argZ[55:48]), .out(adder_15_out[55:48]));  // open: cin, cout
  Adder adder_10 (.a(argY[47:40]), .b(argZ[47:40]), .out(adder_15_out[47:40]));  // open: cin, cout
  Adder adder_11 (.a(argY[39:32]), .b(argZ[39:32]), .out(adder_15_out[39:32]));  // open: cin, cout
  Adder adder_12 (.a(argY[31:24]), .b(argZ[31:24]), .out(adder_15_out[31:24]));  // open: cin, cout
  Adder adder_13 (.a(argY[23:16]), .b(argZ[23:16]), .out(adder_15_out[23:16]));  // open: cin, cout
  Adder adder_14 (.a(argY[15:8]), .b(argZ[15:8]), .out(adder_15_out[15:8]));  // open: cin, cout
  Adder adder_15 (.a(argY[7:0]), .b(argZ[7:0]), .out(adder_15_out[7:0]));  // open: cin, cout
  FPAdder #(.fpwidth(8)) fpadder_8 (.a(argY[63:56]), .b(argZ[63:56]), .out(fpadder_15_out[63:56]));
  FPAdder #(.fpwidth(8)) fpadder_9 (.a(argY[55:48]), .b(argZ[55:48]), .out(fpadder_15_out[55:48]));
  FPAdder #(.fpwidth(8)) fpadder_10 (.a(argY[47:40]), .b(argZ[47:40]), .out(fpadder_15_out[47:40]));
  FPAdder #(.fpwidth(8)) fpadder_11 (.a(argY[39:32]), .b(argZ[39:32]), .out(fpadder_15_out[39:32]));
  FPAdder #(.fpwidth(8)) fpadder_12 (.a(argY[31:24]), .b(argZ[31:24]), .out(fpadder_15_out[31:24]));
  FPAdder #(.fpwidth(8)) fpadder_13 (.a(argY[23:16]), .b(argZ[23:16]), .out(fpadder_15_out[23:16]));
  FPAdder #(.fpwidth(8)) fpadder_14 (.a(argY[15:8]), .b(argZ[15:8]), .out(fpadder_15_out[15:8]));
  FPAdder #(.fpwidth(8)) fpadder_15 (.a(argY[7:0]), .b(argZ[7:0]), .out(fpadder_15_out[7:0]));
  Multiplexer #(.width(16)) multiplexer_49 (
    .in0({16{1'b0}}), .in1(16'h1), .out(multiplexer_49_out[15:0]), .sel(fpcomparator_8_p3));
  Multiplexer #(.width(16)) multiplexer_50 (
    .in0({16{1'b0}}), .in1(16'h1), .out(multiplexer_53_out[63:48]), .sel(fpcomparator_5_p4));
  Multiplexer #(.width(16)) multiplexer_51 (
    .in0({16{1'b0}}), .in1(16'h1), .out(multiplexer_53_out[47:32]), .sel(fpcomparator_6_p4));
  Multiplexer #(.width(16)) multiplexer_52 (
    .in0({16{1'b0}}), .in1(16'h1), .out(multiplexer_53_out[31:16]), .sel(fpcomparator_7_p4));
  Shifter shifter_36 (.in(argY[63:56]), .\dist (bitselector_16_out), .out(shifter_43_out[63:56]));
  Shifter shifter_37 (.in(argY[55:48]), .\dist (bitselector_15_out), .out(shifter_43_out[55:48]));
  Shifter shifter_38 (.in(argY[47:40]), .\dist (bitselector_14_out), .out(shifter_43_out[47:40]));
  Shifter shifter_39 (.in(argY[39:32]), .\dist (bitselector_13_out), .out(shifter_43_out[39:32]));
  Shifter shifter_40 (.in(argY[31:24]), .\dist (bitselector_12_out), .out(shifter_43_out[31:24]));
  Shifter shifter_41 (.in(argY[23:16]), .\dist (bitselector_11_out), .out(shifter_43_out[23:16]));
  Shifter shifter_42 (.in(argY[15:8]), .\dist (bitselector_10_out), .out(shifter_43_out[15:8]));
  Shifter shifter_43 (.in(argY[7:0]), .\dist (bitselector_9_out), .out(shifter_43_out[7:0]));
  Multiplexer #(.width(16)) multiplexer_53 (
    .in0({16{1'b0}}), .in1(16'h1), .out(multiplexer_53_out[15:0]), .sel(fpcomparator_8_p4));
  Subtractor subtractor_8 (.a(argY[63:56]), .b(argZ[63:56]), .out(subtractor_15_out[63:56]));  // open: bin, bout
  Subtractor subtractor_9 (.a(argY[55:48]), .b(argZ[55:48]), .out(subtractor_15_out[55:48]));  // open: bin, bout
  Subtractor subtractor_10 (.a(argY[47:40]), .b(argZ[47:40]), .out(subtractor_15_out[47:40]));  // open: bin, bout
  Subtractor subtractor_11 (.a(argY[39:32]), .b(argZ[39:32]), .out(subtractor_15_out[39:32]));  // open: bin, bout
  Subtractor subtractor_12 (.a(argY[31:24]), .b(argZ[31:24]), .out(subtractor_15_out[31:24]));  // open: bin, bout
  Subtractor subtractor_13 (.a(argY[23:16]), .b(argZ[23:16]), .out(subtractor_15_out[23:16]));  // open: bin, bout
  Subtractor subtractor_14 (.a(argY[15:8]), .b(argZ[15:8]), .out(subtractor_15_out[15:8]));  // open: bin, bout
  Subtractor subtractor_15 (.a(argY[7:0]), .b(argZ[7:0]), .out(subtractor_15_out[7:0]));  // open: bin, bout
  FPSubtractor #(.fpwidth(8)) fpsubtractor_8 (.a(argY[63:56]), .b(argZ[63:56]), .out(fpsubtractor_15_out[63:56]));
  FPSubtractor #(.fpwidth(8)) fpsubtractor_9 (.a(argY[55:48]), .b(argZ[55:48]), .out(fpsubtractor_15_out[55:48]));
  FPSubtractor #(.fpwidth(8)) fpsubtractor_10 (.a(argY[47:40]), .b(argZ[47:40]), .out(fpsubtractor_15_out[47:40]));
  FPSubtractor #(.fpwidth(8)) fpsubtractor_11 (.a(argY[39:32]), .b(argZ[39:32]), .out(fpsubtractor_15_out[39:32]));
  FPSubtractor #(.fpwidth(8)) fpsubtractor_12 (.a(argY[31:24]), .b(argZ[31:24]), .out(fpsubtractor_15_out[31:24]));
  FPSubtractor #(.fpwidth(8)) fpsubtractor_13 (.a(argY[23:16]), .b(argZ[23:16]), .out(fpsubtractor_15_out[23:16]));
  FPSubtractor #(.fpwidth(8)) fpsubtractor_14 (.a(argY[15:8]), .b(argZ[15:8]), .out(fpsubtractor_15_out[15:8]));
  FPSubtractor #(.fpwidth(8)) fpsubtractor_15 (.a(argY[7:0]), .b(argZ[7:0]), .out(fpsubtractor_15_out[7:0]));
  Multiplexer #(.width(16)) multiplexer_54 (
    .in0(argX[63:48]), .in1(buffer_5_out), .out(multiplexer_57_out[63:48]), .sel(not_8_out));
  Multiplexer #(.width(16)) multiplexer_55 (
    .in0(argX[47:32]), .in1(buffer_6_out), .out(multiplexer_57_out[47:32]), .sel(not_9_out));
  assign buffer_5_out = argY[63:48];  // Buffer buffer_5, 16 bits wide
  assign buffer_6_out = argY[47:32];  // Buffer buffer_6, 16 bits wide
  not not_8 (not_8_out, comparator_30_eq);
  Comparator #(.mode("unsigned"), .width(16)) comparator_30 (
    .a(argZ[63:48]), .b({16{1'b0}}), .eq(comparator_30_eq));  // open: gt, lt
  not not_9 (not_9_out, comparator_31_eq);
  Comparator #(.mode("unsigned"), .width(16)) comparator_31 (
    .a(argZ[47:32]), .b({16{1'b0}}), .eq(comparator_31_eq));  // open: gt, lt
  not not_10 (not_10_out, comparator_32_eq);
  Comparator #(.mode("unsigned"), .width(16)) comparator_32 (
    .a(argZ[31:16]), .b({16{1'b0}}), .eq(comparator_32_eq));  // open: gt, lt
  not not_11 (not_11_out, comparator_33_eq);
  Comparator #(.mode("unsigned"), .width(16)) comparator_33 (
    .a(argZ[15:0]), .b({16{1'b0}}), .eq(comparator_33_eq));  // open: gt, lt
  Shifter #(.shift("lr")) shifter_44 (.in(argY[63:56]), .\dist (bitselector_16_out), .out(shifter_51_out[63:56]));
  Shifter #(.shift("lr")) shifter_45 (.in(argY[55:48]), .\dist (bitselector_15_out), .out(shifter_51_out[55:48]));
  Shifter #(.shift("lr")) shifter_46 (.in(argY[47:40]), .\dist (bitselector_14_out), .out(shifter_51_out[47:40]));
  Shifter #(.shift("lr")) shifter_47 (.in(argY[39:32]), .\dist (bitselector_13_out), .out(shifter_51_out[39:32]));
  Shifter #(.shift("lr")) shifter_48 (.in(argY[31:24]), .\dist (bitselector_12_out), .out(shifter_51_out[31:24]));
  Shifter #(.shift("lr")) shifter_49 (.in(argY[23:16]), .\dist (bitselector_11_out), .out(shifter_51_out[23:16]));
  Shifter #(.shift("lr")) shifter_50 (.in(argY[15:8]), .\dist (bitselector_10_out), .out(shifter_51_out[15:8]));
  Shifter #(.shift("lr")) shifter_51 (.in(argY[7:0]), .\dist (bitselector_9_out), .out(shifter_51_out[7:0]));
  Multiplexer #(.width(16)) multiplexer_56 (
    .in0(argX[31:16]), .in1(buffer_7_out), .out(multiplexer_57_out[31:16]), .sel(not_10_out));
  assign buffer_7_out = argY[31:16];  // Buffer buffer_7, 16 bits wide
  Multiplier #(.mode("twosComplement")) multiplier_8 (
    .a(argY[63:56]), .b(argZ[63:56]), .out(multiplier_15_out[63:56]));  // open: cin, cout
  Multiplier #(.mode("twosComplement")) multiplier_9 (
    .a(argY[55:48]), .b(argZ[55:48]), .out(multiplier_15_out[55:48]));  // open: cin, cout
  Multiplier #(.mode("twosComplement")) multiplier_10 (
    .a(argY[47:40]), .b(argZ[47:40]), .out(multiplier_15_out[47:40]));  // open: cin, cout
  Multiplier #(.mode("twosComplement")) multiplier_11 (
    .a(argY[39:32]), .b(argZ[39:32]), .out(multiplier_15_out[39:32]));  // open: cin, cout
  Multiplier #(.mode("twosComplement")) multiplier_12 (
    .a(argY[31:24]), .b(argZ[31:24]), .out(multiplier_15_out[31:24]));  // open: cin, cout
  Multiplier #(.mode("twosComplement")) multiplier_13 (
    .a(argY[23:16]), .b(argZ[23:16]), .out(multiplier_15_out[23:16]));  // open: cin, cout
  Multiplier #(.mode("twosComplement")) multiplier_14 (
    .a(argY[15:8]), .b(argZ[15:8]), .out(multiplier_15_out[15:8]));  // open: cin, cout
  Multiplier #(.mode("twosComplement")) multiplier_15 (
    .a(argY[7:0]), .b(argZ[7:0]), .out(multiplier_15_out[7:0]));  // open: cin, cout
  FPMultiplier #(.fpwidth(8)) fpmultiplier_8 (.a(argY[63:56]), .b(argZ[63:56]), .out(fpmultiplier_15_out[63:56]));
  FPMultiplier #(.fpwidth(8)) fpmultiplier_9 (.a(argY[55:48]), .b(argZ[55:48]), .out(fpmultiplier_15_out[55:48]));
  FPMultiplier #(.fpwidth(8)) fpmultiplier_10 (.a(argY[47:40]), .b(argZ[47:40]), .out(fpmultiplier_15_out[47:40]));
  FPMultiplier #(.fpwidth(8)) fpmultiplier_11 (.a(argY[39:32]), .b(argZ[39:32]), .out(fpmultiplier_15_out[39:32]));
  FPMultiplier #(.fpwidth(8)) fpmultiplier_12 (.a(argY[31:24]), .b(argZ[31:24]), .out(fpmultiplier_15_out[31:24]));
  FPMultiplier #(.fpwidth(8)) fpmultiplier_13 (.a(argY[23:16]), .b(argZ[23:16]), .out(fpmultiplier_15_out[23:16]));
  FPMultiplier #(.fpwidth(8)) fpmultiplier_14 (.a(argY[15:8]), .b(argZ[15:8]), .out(fpmultiplier_15_out[15:8]));
  FPMultiplier #(.fpwidth(8)) fpmultiplier_15 (.a(argY[7:0]), .b(argZ[7:0]), .out(fpmultiplier_15_out[7:0]));
  Multiplexer #(.width(16)) multiplexer_57 (
    .in0(argX[15:0]), .in1(buffer_8_out), .out(multiplexer_57_out[15:0]), .sel(not_11_out));
  assign buffer_8_out = argY[15:0];  // Buffer buffer_8, 16 bits wide
  Comparator comparator_34 (.a(argY[63:56]), .b({8{1'b0}}), .eq(comparator_34_eq), .lt(comparator_34_lt));  // open: gt
  Comparator comparator_35 (.a(argY[55:48]), .b({8{1'b0}}), .eq(comparator_35_eq), .lt(comparator_35_lt));  // open: gt
  Comparator comparator_36 (.a(argY[47:40]), .b({8{1'b0}}), .eq(comparator_36_eq), .lt(comparator_36_lt));  // open: gt
  Comparator comparator_37 (.a(argY[39:32]), .b({8{1'b0}}), .eq(comparator_37_eq), .lt(comparator_37_lt));  // open: gt
  Comparator comparator_38 (.a(argY[31:24]), .b({8{1'b0}}), .eq(comparator_38_eq), .lt(comparator_38_lt));  // open: gt
  Comparator comparator_39 (.a(argY[23:16]), .b({8{1'b0}}), .eq(comparator_39_eq), .lt(comparator_39_lt));  // open: gt
  Comparator comparator_40 (.a(argY[15:8]), .b({8{1'b0}}), .eq(comparator_40_eq), .lt(comparator_40_lt));  // open: gt
  Comparator comparator_41 (.a(argY[7:0]), .b({8{1'b0}}), .eq(comparator_41_eq), .lt(comparator_41_lt));  // open: gt
  Shifter #(.shift("ar")) shifter_52 (.in(argY[63:56]), .\dist (bitselector_16_out), .out(shifter_59_out[63:56]));
  Shifter #(.shift("ar")) shifter_53 (.in(argY[55:48]), .\dist (bitselector_15_out), .out(shifter_59_out[55:48]));
  Shifter #(.shift("ar")) shifter_54 (.in(argY[47:40]), .\dist (bitselector_14_out), .out(shifter_59_out[47:40]));
  Shifter #(.shift("ar")) shifter_55 (.in(argY[39:32]), .\dist (bitselector_13_out), .out(shifter_59_out[39:32]));
  Shifter #(.shift("ar")) shifter_56 (.in(argY[31:24]), .\dist (bitselector_12_out), .out(shifter_59_out[31:24]));
  Shifter #(.shift("ar")) shifter_57 (.in(argY[23:16]), .\dist (bitselector_11_out), .out(shifter_59_out[23:16]));
  Shifter #(.shift("ar")) shifter_58 (.in(argY[15:8]), .\dist (bitselector_10_out), .out(shifter_59_out[15:8]));
  Shifter #(.shift("ar")) shifter_59 (.in(argY[7:0]), .\dist (bitselector_9_out), .out(shifter_59_out[7:0]));
  Multiplexer #(.width(8)) multiplexer_58 (
    .in0({8{1'b0}}), .in1(8'h1), .out(multiplexer_65_out[63:56]), .sel(comparator_34_eq));
  Divider #(.mode("twosComplement")) divider_8 (
    .a(argY[63:56]), .b(argZ[63:56]), .out(divider_15_out[63:56]));  // open: upper, rem
  Divider #(.mode("twosComplement")) divider_9 (
    .a(argY[55:48]), .b(argZ[55:48]), .out(divider_15_out[55:48]));  // open: upper, rem
  Divider #(.mode("twosComplement")) divider_10 (
    .a(argY[47:40]), .b(argZ[47:40]), .out(divider_15_out[47:40]));  // open: upper, rem
  Divider #(.mode("twosComplement")) divider_11 (
    .a(argY[39:32]), .b(argZ[39:32]), .out(divider_15_out[39:32]));  // open: upper, rem
  Divider #(.mode("twosComplement")) divider_12 (
    .a(argY[31:24]), .b(argZ[31:24]), .out(divider_15_out[31:24]));  // open: upper, rem
  Divider #(.mode("twosComplement")) divider_13 (
    .a(argY[23:16]), .b(argZ[23:16]), .out(divider_15_out[23:16]));  // open: upper, rem
  Divider #(.mode("twosComplement")) divider_14 (
    .a(argY[15:8]), .b(argZ[15:8]), .out(divider_15_out[15:8]));  // open: upper, rem
  Divider #(.mode("twosComplement")) divider_15 (
    .a(argY[7:0]), .b(argZ[7:0]), .out(divider_15_out[7:0]));  // open: upper, rem
  FPDivider #(.fpwidth(8)) fpdivider_8 (.a(argY[63:56]), .b(argZ[63:56]), .out(fpdivider_15_out[63:56]));
  FPDivider #(.fpwidth(8)) fpdivider_9 (.a(argY[55:48]), .b(argZ[55:48]), .out(fpdivider_15_out[55:48]));
  FPDivider #(.fpwidth(8)) fpdivider_10 (.a(argY[47:40]), .b(argZ[47:40]), .out(fpdivider_15_out[47:40]));
  FPDivider #(.fpwidth(8)) fpdivider_11 (.a(argY[39:32]), .b(argZ[39:32]), .out(fpdivider_15_out[39:32]));
  FPDivider #(.fpwidth(8)) fpdivider_12 (.a(argY[31:24]), .b(argZ[31:24]), .out(fpdivider_15_out[31:24]));
  FPDivider #(.fpwidth(8)) fpdivider_13 (.a(argY[23:16]), .b(argZ[23:16]), .out(fpdivider_15_out[23:16]));
  FPDivider #(.fpwidth(8)) fpdivider_14 (.a(argY[15:8]), .b(argZ[15:8]), .out(fpdivider_15_out[15:8]));
  FPDivider #(.fpwidth(8)) fpdivider_15 (.a(argY[7:0]), .b(argZ[7:0]), .out(fpdivider_15_out[7:0]));
  Multiplexer #(.width(8)) multiplexer_59 (
    .in0({8{1'b0}}), .in1(8'h1), .out(multiplexer_65_out[55:48]), .sel(comparator_35_eq));
  Multiplexer #(.width(8)) multiplexer_60 (
    .in0({8{1'b0}}), .in1(8'h1), .out(multiplexer_65_out[47:40]), .sel(comparator_36_eq));
  Multiplexer #(.width(8)) multiplexer_61 (
    .in0({8{1'b0}}), .in1(8'h1), .out(multiplexer_65_out[39:32]), .sel(comparator_37_eq));
  Multiplexer #(.width(8)) multiplexer_62 (
    .in0({8{1'b0}}), .in1(8'h1), .out(multiplexer_65_out[31:24]), .sel(comparator_38_eq));
  Shifter #(.shift("rl")) shifter_60 (.in(argY[63:56]), .\dist (bitselector_16_out), .out(shifter_67_out[63:56]));
  Shifter #(.shift("rl")) shifter_61 (.in(argY[55:48]), .\dist (bitselector_15_out), .out(shifter_67_out[55:48]));
  Shifter #(.shift("rl")) shifter_62 (.in(argY[47:40]), .\dist (bitselector_14_out), .out(shifter_67_out[47:40]));
  Shifter #(.shift("rl")) shifter_63 (.in(argY[39:32]), .\dist (bitselector_13_out), .out(shifter_67_out[39:32]));
  Shifter #(.shift("rl")) shifter_64 (.in(argY[31:24]), .\dist (bitselector_12_out), .out(shifter_67_out[31:24]));
  Shifter #(.shift("rl")) shifter_65 (.in(argY[23:16]), .\dist (bitselector_11_out), .out(shifter_67_out[23:16]));
  Shifter #(.shift("rl")) shifter_66 (.in(argY[15:8]), .\dist (bitselector_10_out), .out(shifter_67_out[15:8]));
  Shifter #(.shift("rl")) shifter_67 (.in(argY[7:0]), .\dist (bitselector_9_out), .out(shifter_67_out[7:0]));
  Multiplexer #(.width(8)) multiplexer_63 (
    .in0({8{1'b0}}), .in1(8'h1), .out(multiplexer_65_out[23:16]), .sel(comparator_39_eq));
  Multiplexer #(.width(8)) multiplexer_64 (
    .in0({8{1'b0}}), .in1(8'h1), .out(multiplexer_65_out[15:8]), .sel(comparator_40_eq));
  Negator negator_8 (.in(argY[63:56]), .out(negator_15_out[63:56]));
  Negator negator_9 (.in(argY[55:48]), .out(negator_15_out[55:48]));
  Negator negator_10 (.in(argY[47:40]), .out(negator_15_out[47:40]));
  Negator negator_11 (.in(argY[39:32]), .out(negator_15_out[39:32]));
  Negator negator_12 (.in(argY[31:24]), .out(negator_15_out[31:24]));
  Negator negator_13 (.in(argY[23:16]), .out(negator_15_out[23:16]));
  Negator negator_14 (.in(argY[15:8]), .out(negator_15_out[15:8]));
  Negator negator_15 (.in(argY[7:0]), .out(negator_15_out[7:0]));
  // FPNegator #(.fpwidth(8)) fpnegator_8: pin names not known; wires that end beside it: argY[63:56], fpnegator_15_p18[63:56]
  // FPNegator #(.fpwidth(8)) fpnegator_9: pin names not known; wires that end beside it: argY[55:48], fpnegator_15_p18[55:48]
  // FPNegator #(.fpwidth(8)) fpnegator_10: pin names not known; wires that end beside it: argY[47:40], fpnegator_15_p18[47:40]
  // FPNegator #(.fpwidth(8)) fpnegator_11: pin names not known; wires that end beside it: argY[39:32], fpnegator_15_p18[39:32]
  // FPNegator #(.fpwidth(8)) fpnegator_12: pin names not known; wires that end beside it: argY[31:24], fpnegator_15_p18[31:24]
  // FPNegator #(.fpwidth(8)) fpnegator_13: pin names not known; wires that end beside it: argY[23:16], fpnegator_15_p18[23:16]
  // FPNegator #(.fpwidth(8)) fpnegator_14: pin names not known; wires that end beside it: argY[15:8], fpnegator_15_p18[15:8]
  // FPNegator #(.fpwidth(8)) fpnegator_15: pin names not known; wires that end beside it: argY[7:0], argY[7:0], argY[15:8], argY[23:16], argY[31:24], argY[39:32], argY[47:40], argY[55:48], argY[63:56], argZ[7:0], argZ[15:8], argZ[23:16], argZ[31:24], argZ[39:32], argZ[47:40], argZ[55:48], argZ[63:56], fpnegator_15_p18[7:0]
  Multiplexer #(.width(8)) multiplexer_65 (
    .in0({8{1'b0}}), .in1(8'h1), .out(multiplexer_65_out[7:0]), .sel(comparator_41_eq));
  Multiplexer #(.width(8)) multiplexer_66 (
    .in0({8{1'b0}}), .in1(8'h1), .out(multiplexer_73_out[63:56]), .sel(comparator_34_lt));
  Shifter #(.shift("rr")) shifter_68 (.in(argY[63:56]), .\dist (bitselector_16_out), .out(shifter_75_out[63:56]));
  Shifter #(.shift("rr")) shifter_69 (.in(argY[55:48]), .\dist (bitselector_15_out), .out(shifter_75_out[55:48]));
  Shifter #(.shift("rr")) shifter_70 (.in(argY[47:40]), .\dist (bitselector_14_out), .out(shifter_75_out[47:40]));
  Shifter #(.shift("rr")) shifter_71 (.in(argY[39:32]), .\dist (bitselector_13_out), .out(shifter_75_out[39:32]));
  Shifter #(.shift("rr")) shifter_72 (.in(argY[31:24]), .\dist (bitselector_12_out), .out(shifter_75_out[31:24]));
  Shifter #(.shift("rr")) shifter_73 (.in(argY[23:16]), .\dist (bitselector_11_out), .out(shifter_75_out[23:16]));
  Shifter #(.shift("rr")) shifter_74 (.in(argY[15:8]), .\dist (bitselector_10_out), .out(shifter_75_out[15:8]));
  Shifter #(.shift("rr")) shifter_75 (.in(argY[7:0]), .\dist (bitselector_9_out), .out(shifter_75_out[7:0]));
  Multiplexer #(.width(8)) multiplexer_67 (
    .in0({8{1'b0}}), .in1(8'h1), .out(multiplexer_73_out[55:48]), .sel(comparator_35_lt));
  Multiplexer #(.width(8)) multiplexer_68 (
    .in0({8{1'b0}}), .in1(8'h1), .out(multiplexer_73_out[47:40]), .sel(comparator_36_lt));
  Multiplexer #(.width(8)) multiplexer_69 (
    .in0({8{1'b0}}), .in1(8'h1), .out(multiplexer_73_out[39:32]), .sel(comparator_37_lt));
  Multiplexer #(.width(8)) multiplexer_70 (
    .in0({8{1'b0}}), .in1(8'h1), .out(multiplexer_73_out[31:24]), .sel(comparator_38_lt));
  Multiplexer #(.width(8)) multiplexer_71 (
    .in0({8{1'b0}}), .in1(8'h1), .out(multiplexer_73_out[23:16]), .sel(comparator_39_lt));
  Multiplexer #(.width(8)) multiplexer_72 (
    .in0({8{1'b0}}), .in1(8'h1), .out(multiplexer_73_out[15:8]), .sel(comparator_40_lt));
  Multiplexer #(.width(8)) multiplexer_73 (
    .in0({8{1'b0}}), .in1(8'h1), .out(multiplexer_73_out[7:0]), .sel(comparator_41_lt));
  // FPComparator #(.fpwidth(8)) fpcomparator_9: pin names not known; wires that end beside it: argY[63:56], {8{1'b0}}, fpcomparator_9_p3, fpcomparator_9_p4
  // FPComparator #(.fpwidth(8)) fpcomparator_10: pin names not known; wires that end beside it: argY[55:48], {8{1'b0}}, fpcomparator_10_p3, fpcomparator_10_p4
  // FPComparator #(.fpwidth(8)) fpcomparator_11: pin names not known; wires that end beside it: argY[47:40], {8{1'b0}}, fpcomparator_11_p3, fpcomparator_11_p4
  // FPComparator #(.fpwidth(8)) fpcomparator_12: pin names not known; wires that end beside it: argY[39:32], {8{1'b0}}, fpcomparator_12_p3, fpcomparator_12_p4
  // FPComparator #(.fpwidth(8)) fpcomparator_13: pin names not known; wires that end beside it: argY[31:24], {8{1'b0}}, fpcomparator_13_p3, fpcomparator_13_p4
  // FPComparator #(.fpwidth(8)) fpcomparator_14: pin names not known; wires that end beside it: argY[23:16], {8{1'b0}}, fpcomparator_14_p3, fpcomparator_14_p4
  // FPComparator #(.fpwidth(8)) fpcomparator_15: pin names not known; wires that end beside it: argY[15:8], {8{1'b0}}, fpcomparator_15_p3, fpcomparator_15_p4
  // FPComparator #(.fpwidth(8)) fpcomparator_16: pin names not known; wires that end beside it: argY[7:0], {8{1'b0}}, fpcomparator_16_p3, fpcomparator_16_p4
  Multiplexer #(.width(8)) multiplexer_74 (
    .in0({8{1'b0}}), .in1(8'h1), .out(multiplexer_81_out[63:56]), .sel(fpcomparator_9_p3));
  Multiplexer #(.width(8)) multiplexer_75 (
    .in0({8{1'b0}}), .in1(8'h1), .out(multiplexer_81_out[55:48]), .sel(fpcomparator_10_p3));
  Multiplexer #(.width(8)) multiplexer_76 (
    .in0({8{1'b0}}), .in1(8'h1), .out(multiplexer_81_out[47:40]), .sel(fpcomparator_11_p3));
  Multiplexer #(.width(8)) multiplexer_77 (
    .in0({8{1'b0}}), .in1(8'h1), .out(multiplexer_81_out[39:32]), .sel(fpcomparator_12_p3));
  Multiplexer #(.width(8)) multiplexer_78 (
    .in0({8{1'b0}}), .in1(8'h1), .out(multiplexer_81_out[31:24]), .sel(fpcomparator_13_p3));
  Multiplexer #(.width(8)) multiplexer_79 (
    .in0({8{1'b0}}), .in1(8'h1), .out(multiplexer_81_out[23:16]), .sel(fpcomparator_14_p3));
  Multiplexer #(.width(8)) multiplexer_80 (
    .in0({8{1'b0}}), .in1(8'h1), .out(multiplexer_81_out[15:8]), .sel(fpcomparator_15_p3));
  Multiplexer #(.width(8)) multiplexer_81 (
    .in0({8{1'b0}}), .in1(8'h1), .out(multiplexer_81_out[7:0]), .sel(fpcomparator_16_p3));
  Multiplexer #(.width(8)) multiplexer_82 (
    .in0({8{1'b0}}), .in1(8'h1), .out(multiplexer_89_out[63:56]), .sel(fpcomparator_9_p4));
  Multiplexer #(.width(8)) multiplexer_83 (
    .in0({8{1'b0}}), .in1(8'h1), .out(multiplexer_89_out[55:48]), .sel(fpcomparator_10_p4));
  Multiplexer #(.width(8)) multiplexer_84 (
    .in0({8{1'b0}}), .in1(8'h1), .out(multiplexer_89_out[47:40]), .sel(fpcomparator_11_p4));
  Multiplexer #(.width(8)) multiplexer_85 (
    .in0({8{1'b0}}), .in1(8'h1), .out(multiplexer_89_out[39:32]), .sel(fpcomparator_12_p4));
  Multiplexer #(.width(8)) multiplexer_86 (
    .in0({8{1'b0}}), .in1(8'h1), .out(multiplexer_89_out[31:24]), .sel(fpcomparator_13_p4));
  Multiplexer #(.width(8)) multiplexer_87 (
    .in0({8{1'b0}}), .in1(8'h1), .out(multiplexer_89_out[23:16]), .sel(fpcomparator_14_p4));
  Multiplexer #(.width(8)) multiplexer_88 (
    .in0({8{1'b0}}), .in1(8'h1), .out(multiplexer_89_out[15:8]), .sel(fpcomparator_15_p4));
  Multiplexer #(.width(8)) multiplexer_89 (
    .in0({8{1'b0}}), .in1(8'h1), .out(multiplexer_89_out[7:0]), .sel(fpcomparator_16_p4));
  Multiplexer #(.width(8)) multiplexer_90 (
    .in0(argX[63:56]), .in1(buffer_9_out), .out(multiplexer_97_out[63:56]), .sel(not_12_out));
  assign buffer_9_out = argY[63:56];  // Buffer buffer_9, 8 bits wide
  Multiplexer #(.width(8)) multiplexer_91 (
    .in0(argX[55:48]), .in1(buffer_10_out), .out(multiplexer_97_out[55:48]), .sel(not_13_out));
  assign buffer_10_out = argY[55:48];  // Buffer buffer_10, 8 bits wide
  not not_12 (not_12_out, comparator_42_eq);
  Comparator #(.mode("unsigned")) comparator_42 (
    .a(argZ[63:56]), .b({8{1'b0}}), .eq(comparator_42_eq));  // open: gt, lt
  not not_13 (not_13_out, comparator_43_eq);
  Comparator #(.mode("unsigned")) comparator_43 (
    .a(argZ[55:48]), .b({8{1'b0}}), .eq(comparator_43_eq));  // open: gt, lt
  not not_14 (not_14_out, comparator_44_eq);
  Comparator #(.mode("unsigned")) comparator_44 (
    .a(argZ[47:40]), .b({8{1'b0}}), .eq(comparator_44_eq));  // open: gt, lt
  not not_15 (not_15_out, comparator_45_eq);
  Comparator #(.mode("unsigned")) comparator_45 (
    .a(argZ[39:32]), .b({8{1'b0}}), .eq(comparator_45_eq));  // open: gt, lt
  not not_16 (not_16_out, comparator_46_eq);
  Comparator #(.mode("unsigned")) comparator_46 (
    .a(argZ[31:24]), .b({8{1'b0}}), .eq(comparator_46_eq));  // open: gt, lt
  not not_17 (not_17_out, comparator_47_eq);
  Comparator #(.mode("unsigned")) comparator_47 (
    .a(argZ[23:16]), .b({8{1'b0}}), .eq(comparator_47_eq));  // open: gt, lt
  not not_18 (not_18_out, comparator_48_eq);
  Comparator #(.mode("unsigned")) comparator_48 (.a(argZ[15:8]), .b({8{1'b0}}), .eq(comparator_48_eq));  // open: gt, lt
  not not_19 (not_19_out, comparator_49_eq);
  Comparator #(.mode("unsigned")) comparator_49 (.a(argZ[7:0]), .b({8{1'b0}}), .eq(comparator_49_eq));  // open: gt, lt
  Multiplexer #(.width(8)) multiplexer_92 (
    .in0(argX[47:40]), .in1(buffer_11_out), .out(multiplexer_97_out[47:40]), .sel(not_14_out));
  Multiplexer #(.width(8)) multiplexer_93 (
    .in0(argX[39:32]), .in1(buffer_12_out), .out(multiplexer_97_out[39:32]), .sel(not_15_out));
  assign buffer_11_out = argY[47:40];  // Buffer buffer_11, 8 bits wide
  Multiplexer #(.width(8)) multiplexer_94 (
    .in0(argX[31:24]), .in1(buffer_13_out), .out(multiplexer_97_out[31:24]), .sel(not_16_out));
  assign buffer_12_out = argY[39:32];  // Buffer buffer_12, 8 bits wide
  assign buffer_13_out = argY[31:24];  // Buffer buffer_13, 8 bits wide
  Multiplexer #(.width(8)) multiplexer_95 (
    .in0(argX[23:16]), .in1(buffer_14_out), .out(multiplexer_97_out[23:16]), .sel(not_17_out));
  assign buffer_14_out = argY[23:16];  // Buffer buffer_14, 8 bits wide
  Multiplexer #(.width(8)) multiplexer_96 (
    .in0(argX[15:8]), .in1(buffer_15_out), .out(multiplexer_97_out[15:8]), .sel(not_18_out));
  Multiplexer #(.width(8)) multiplexer_97 (
    .in0(argX[7:0]), .in1(buffer_16_out), .out(multiplexer_97_out[7:0]), .sel(not_19_out));
  assign buffer_15_out = argY[15:8];  // Buffer buffer_15, 8 bits wide
  assign buffer_16_out = argY[7:0];  // Buffer buffer_16, 8 bits wide
endmodule
